// Logisim project Computer.circ as structural Verilog: 2 circuits, main circuit Computer
module Computer (
);

  wire clock_1_out, cpu_1_writem, Reset_out, rgb_video_1_p3, sm_1_selkeyboard;
  wire [7:0] rgb_video_1_p5;
  wire [8:0] rgb_video_1_p4;
  wire [14:0] cpu_1_addressm;
  wire [15:0] cpu_1_aluout, cpu_1_prc, DATA_dout, Instructions_data, keyboard_1_data, multiplexer_1_out;

  ROM #(.addrWidth(16), .dataWidth(16)) Instructions (.addr(cpu_1_prc), .data(Instructions_data));
  Button Reset (.out(Reset_out));
  CPU cpu_1 (
    .INSTRUCTION(Instructions_data), .inM(multiplexer_1_out), .RESET(Reset_out), .ALUout(cpu_1_aluout),
    .PRC(cpu_1_prc), .WriteM(cpu_1_writem), .AddressM(cpu_1_addressm));
  Clock clock_1 (.out(clock_1_out));
  RAM #(.addrWidth(15), .clearpin("true"), .dataWidth(16), .enables("line")) DATA (
    .addr(cpu_1_addressm), .we(cpu_1_writem), .clk(clock_1_out), .din(cpu_1_aluout), .dout(DATA_dout),
    .clr(Reset_out));
  Keyboard #(.buflen(1)) keyboard_1 (
    .clk(clock_1_out), .re(sm_1_selkeyboard), .clr(Reset_out), .data(keyboard_1_data[6:0]));  // open: avail
  // RGB_Video #(.cursor("No Cursor"), .height(256), .width(512), .writemode("Packed 16 (1bpp)")) rgb_video_1: pin names not known; wires that end beside it: Reset_out, clock_1_out, rgb_video_1_p3, rgb_video_1_p4, rgb_video_1_p5, cpu_1_aluout
  SM sm_1 (
    .address(cpu_1_addressm), .CPUEnableWrite(cpu_1_writem), .SelKeyBoard(sm_1_selkeyboard),
    .WriteToScreen(rgb_video_1_p3), .PY(rgb_video_1_p5), .PX(rgb_video_1_p4));
  Multiplexer #(.width(16)) multiplexer_1 (
    .in0(DATA_dout), .in1(keyboard_1_data), .out(multiplexer_1_out), .sel(sm_1_selkeyboard));
  // Pins of 7 and 16 bits meet at keyboard_1_data

  // Notes on the sheet:
  //   contents of Instructions (hex, n*v repeats v):
  //   0 fc10 17 e306 10 e308 4000 ec10 11 e308 11 fc20 ee88 11 fc10 20 e090 11 e308 10 fc98 a e301 17 ea87
endmodule

module SM (
  input  [14:0] address,
  input  CPUEnableWrite,
  output WriteToScreen,
  output [7:0] PY,
  output [8:0] PX,
  output SelKeyBoard
);

  wire and_1_out, comparator_1_eq, comparator_1_gt, not_1_out, or_1_out;
  wire [1:0] pull_resistor_1_node;
  wire [14:0] subtractor_1_out;

  or or_1 (or_1_out, comparator_1_gt, comparator_1_eq);
  Comparator #(.mode("unsigned"), .width(15)) comparator_1 (
    .a(address), .b(15'h4000), .gt(comparator_1_gt), .eq(comparator_1_eq));  // open: lt
  not not_1 (not_1_out, SelKeyBoard);
  Comparator #(.mode("unsigned"), .width(15)) comparator_2 (
    .a(address), .b(15'h6000), .eq(SelKeyBoard));  // open: gt, lt
  Subtractor #(.width(15)) subtractor_1 (.a(address), .b(15'h4000), .out(subtractor_1_out));  // open: bin, bout
  and and_1 (and_1_out, or_1_out, not_1_out);
  Pull_Resistor pull_resistor_1 (.node(pull_resistor_1_node));
  and and_2 (WriteToScreen, CPUEnableWrite, and_1_out);
  Shifter #(.width(17)) shifter_1 (.in({pull_resistor_1_node, subtractor_1_out}), .\dist (5'b00100), .out({PY, PX}));
endmodule
