// Logisim project CPU.circ as structural Verilog: 5 circuits, main circuit CPU
module CPU (
  input  [15:0] INSTRUCTION,
  input  [15:0] inM,
  input  RESET,
  output [15:0] ALUout,
  output [14:0] AddressM,
  output WriteM,
  output [15:0] PRC
);

  wire alu_1_ng, alu_1_zr, clock_1_out, cu_1_cmuxalu, cu_1_cmuxinstruction, cu_1_jmp, cu_1_la, cu_1_ld;
  wire [5:0] cu_1_calu;
  wire [15:0] multiplexer_1_out, multiplexer_2_out, register_2_q;
  wire [15:15] register_1_q;

  Clock clock_1 (.out(clock_1_out));
  Register #(.width(16)) register_1 (
    .D(multiplexer_1_out), .en(cu_1_la), .clk(clock_1_out), .Q({register_1_q[15], AddressM}), .clr(RESET));
  Multiplexer #(.width(16)) multiplexer_1 (
    .in0(INSTRUCTION), .in1(ALUout), .out(multiplexer_1_out), .sel(cu_1_cmuxinstruction));
  Register #(.width(16)) register_2 (.D(ALUout), .en(cu_1_ld), .clk(clock_1_out), .Q(register_2_q), .clr(RESET));
  Multiplexer #(.width(16)) multiplexer_2 (
    .in0({register_1_q[15], AddressM}), .in1(inM), .out(multiplexer_2_out), .sel(cu_1_cmuxalu));
  PC pc_1 (
    .ck(clock_1_out), .reset(RESET), .load(cu_1_jmp), .inc(1'b1), .in_1({register_1_q[15], AddressM}),
    .out_6(PRC));
  ALU alu_1 (
    .X(register_2_q), .Y(multiplexer_2_out), .zx(cu_1_calu[0]), .nx(cu_1_calu[1]), .zy(cu_1_calu[2]),
    .ny(cu_1_calu[3]), .f(cu_1_calu[4]), .no(cu_1_calu[5]), .zr(alu_1_zr), .out_9(ALUout), .ng(alu_1_ng));
  CU cu_1 (
    .zr(alu_1_zr), .in_1(INSTRUCTION), .ng(alu_1_ng), .JMP(cu_1_jmp), .CMUXinstruction(cu_1_cmuxinstruction),
    .CMUXALU(cu_1_cmuxalu), .CALU(cu_1_calu), .WM(WriteM), .LD(cu_1_ld), .LA(cu_1_la));
  Pull_Resistor pull_resistor_1 (.node(register_1_q[15]));
endmodule

module ALU (
  input  zx,
  input  nx,
  input  zy,
  input  ny,
  input  f,
  input  no,
  input  [15:0] X,
  input  [15:0] Y,
  output [15:0] out_9,
  output zr,
  output ng
);

  wire adder16_1_out_5, or_1_out;
  wire [15:0] adder16_1_out_4, and_1_out, multiplexer_1_out, multiplexer_2_out, multiplexer_3_out,
       multiplexer_4_out, multiplexer_5_out, not_1_out, not_2_out, not_3_out;

  Multiplexer #(.width(16)) multiplexer_1 (.in0(X), .in1({16{1'b0}}), .out(multiplexer_1_out), .sel(zx));
  Multiplexer #(.width(16)) multiplexer_2 (.in0(Y), .in1({16{1'b0}}), .out(multiplexer_2_out), .sel(zy));
  Multiplexer #(.width(16)) multiplexer_3 (.in0(multiplexer_1_out), .in1(not_1_out), .out(multiplexer_3_out), .sel(nx));
  assign not_1_out = ~multiplexer_1_out;  // NOT_Gate not_1, 16 bits wide
  Multiplexer #(.width(16)) multiplexer_4 (.in0(multiplexer_2_out), .in1(not_2_out), .out(multiplexer_4_out), .sel(ny));
  assign not_2_out = ~multiplexer_2_out;  // NOT_Gate not_2, 16 bits wide
  assign and_1_out = multiplexer_3_out & multiplexer_4_out;  // AND_Gate and_1, 16 bits wide
  ADDER16 adder16_1 (
    .in_2(multiplexer_3_out), .in_3(1'b0), .in_1(multiplexer_4_out), .out_5(adder16_1_out_5),
    .out_4(adder16_1_out_4));
  Multiplexer #(.width(16)) multiplexer_5 (.in0(and_1_out), .in1(adder16_1_out_4), .out(multiplexer_5_out), .sel(f));
  Pull_Resistor pull_resistor_1 (.node(adder16_1_out_5));
  Multiplexer #(.width(16)) multiplexer_6 (.in0(multiplexer_5_out), .in1(not_3_out), .out({ng, out_9[14:0]}), .sel(no));
  assign not_3_out = ~multiplexer_5_out;  // NOT_Gate not_3, 16 bits wide
  or or_1 (or_1_out, out_9[0], out_9[1], out_9[2], out_9[3], out_9[4], out_9[5], out_9[6], out_9[7], out_9[8], out_9[9], out_9[10], out_9[11], out_9[12], out_9[13], out_9[14], ng);
  not not_4 (zr, or_1_out);

  assign out_9[15] = ng;
endmodule

module CU (
  input  [15:0] in_1,
  input  ng,
  input  zr,
  output CMUXinstruction,
  output CMUXALU,
  output [5:0] CALU,
  output WM,
  output LD,
  output LA,
  output JMP
);

  wire and_1_out, and_2_out, and_3_out, and_4_out, and_5_out, and_6_out, demultiplexer_1_out0,
       demultiplexer_1_out1, demultiplexer_1_out2, demultiplexer_1_out3, demultiplexer_1_out4,
       demultiplexer_1_out5, demultiplexer_1_out6, demultiplexer_1_out7, not_1_out, not_2_out, not_3_out,
       or_1_out;
  wire [7:0] demultiplexer_2_out0;

  Pull_Resistor pull_resistor_1 (.node(in_1[14]));
  Pull_Resistor pull_resistor_2 (.node(in_1[13]));
  not not_1 (not_1_out, in_1[15]);
  Demultiplexer #(.select(3)) demultiplexer_1 (
    .out0(demultiplexer_1_out0), .out1(demultiplexer_1_out1), .out2(demultiplexer_1_out2),
    .out3(demultiplexer_1_out3), .out4(demultiplexer_1_out4), .out5(demultiplexer_1_out5),
    .out6(demultiplexer_1_out6), .out7(demultiplexer_1_out7), .in(in_1[15]), .sel(in_1[5:3]));
  Pull_Resistor pull_resistor_3 (.node(demultiplexer_1_out0));
  Demultiplexer #(.select(3)) demultiplexer_2 (
    .out0(demultiplexer_2_out0[0]), .out1(demultiplexer_2_out0[1]), .out2(demultiplexer_2_out0[2]),
    .out3(demultiplexer_2_out0[3]), .out4(demultiplexer_2_out0[4]), .out5(demultiplexer_2_out0[5]),
    .out6(demultiplexer_2_out0[6]), .out7(demultiplexer_2_out0[7]), .in(in_1[15]), .sel(in_1[2:0]));
  or M (WM, demultiplexer_1_out1, demultiplexer_1_out3, demultiplexer_1_out5, demultiplexer_1_out7);
  or D (LD, demultiplexer_1_out7, demultiplexer_1_out3, demultiplexer_1_out2, demultiplexer_1_out6);
  or A (LA, demultiplexer_1_out7, demultiplexer_1_out5, not_1_out, demultiplexer_1_out4, demultiplexer_1_out6);
  Pull_Resistor pull_resistor_4 (.node(demultiplexer_2_out0[0]));
  not not_2 (not_2_out, zr);
  not not_3 (not_3_out, ng);
  and and_1 (and_1_out, demultiplexer_2_out0[1], not_2_out, not_3_out);
  and and_2 (and_2_out, demultiplexer_2_out0[2], zr);
  and and_3 (and_3_out, demultiplexer_2_out0[3], not_3_out);
  and and_4 (and_4_out, demultiplexer_2_out0[4], ng);
  and and_5 (and_5_out, demultiplexer_2_out0[5], not_2_out);
  and and_6 (and_6_out, demultiplexer_2_out0[6], or_1_out);
  or or_1 (or_1_out, ng, zr);
  or or_2 (JMP, and_1_out, and_2_out, and_3_out, and_4_out, and_5_out, and_6_out, demultiplexer_2_out0[7]);

  assign CALU = {in_1[6], in_1[7], in_1[8], in_1[9], in_1[10], in_1[11]};
  assign CMUXALU = in_1[12];
  assign CMUXinstruction = in_1[15];
endmodule

module PC (
  input  [15:0] in_1,
  input  ck,
  input  reset,
  input  load,
  input  inc,
  output [15:0] out_6
);

  wire and_1_out, and_2_out, and_3_out, and_4_out, and_5_out, and_6_out, and_7_out, and_8_out, and_9_out,
       and_10_out, and_11_out, and_12_out, and_13_out, and_14_out, d_ff_1_qn, multiplexer_1_out,
       multiplexer_2_out, multiplexer_3_out, multiplexer_4_out, multiplexer_5_out, multiplexer_6_out,
       multiplexer_7_out, multiplexer_8_out, multiplexer_9_out, multiplexer_10_out, multiplexer_11_out,
       multiplexer_12_out, multiplexer_13_out, multiplexer_14_out, multiplexer_15_out, multiplexer_16_out,
       multiplexer_17_out, multiplexer_18_out, multiplexer_19_out, multiplexer_20_out, multiplexer_21_out,
       multiplexer_22_out, multiplexer_23_out, multiplexer_24_out, multiplexer_25_out, multiplexer_26_out,
       multiplexer_27_out, multiplexer_28_out, multiplexer_29_out, multiplexer_30_out, multiplexer_31_out,
       multiplexer_32_out, multiplexer_33_out, multiplexer_34_out, multiplexer_35_out, multiplexer_36_out,
       multiplexer_37_out, multiplexer_38_out, multiplexer_39_out, multiplexer_40_out, multiplexer_41_out,
       multiplexer_42_out, multiplexer_43_out, multiplexer_44_out, multiplexer_45_out, multiplexer_46_out,
       multiplexer_47_out, multiplexer_48_out, xor_1_out, xor_2_out, xor_3_out, xor_4_out, xor_5_out,
       xor_6_out, xor_7_out, xor_8_out, xor_9_out, xor_10_out, xor_11_out, xor_12_out, xor_13_out,
       xor_14_out, xor_15_out;

  Multiplexer multiplexer_1 (.in0(out_6[0]), .in1(d_ff_1_qn), .out(multiplexer_1_out), .sel(inc));
  Multiplexer multiplexer_2 (.in0(multiplexer_1_out), .in1(in_1[0]), .out(multiplexer_2_out), .sel(load));
  D_Flip_Flop d_ff_1 (.D(multiplexer_3_out), .clk(ck), .Q(out_6[0]), .Qn(d_ff_1_qn), .reset(reset));  // open: preset
  Multiplexer multiplexer_3 (.in0(multiplexer_2_out), .in1(1'b0), .out(multiplexer_3_out), .sel(reset));
  and and_1 (and_1_out, out_6[1], out_6[0]);
  Multiplexer multiplexer_4 (.in0(out_6[1]), .in1(xor_1_out), .out(multiplexer_4_out), .sel(inc));
  xor xor_1 (xor_1_out, out_6[0], out_6[1]);
  Multiplexer multiplexer_5 (.in0(multiplexer_4_out), .in1(in_1[1]), .out(multiplexer_5_out), .sel(load));
  D_Flip_Flop d_ff_2 (.D(multiplexer_6_out), .clk(ck), .Q(out_6[1]), .reset(reset));  // open: Qn, preset
  Multiplexer multiplexer_6 (.in0(multiplexer_5_out), .in1(1'b0), .out(multiplexer_6_out), .sel(reset));
  and and_2 (and_2_out, out_6[2], and_1_out);
  Multiplexer multiplexer_7 (.in0(out_6[2]), .in1(xor_2_out), .out(multiplexer_7_out), .sel(inc));
  xor xor_2 (xor_2_out, and_1_out, out_6[2]);
  Multiplexer multiplexer_8 (.in0(multiplexer_7_out), .in1(in_1[2]), .out(multiplexer_8_out), .sel(load));
  Multiplexer multiplexer_9 (.in0(multiplexer_8_out), .in1(1'b0), .out(multiplexer_9_out), .sel(reset));
  D_Flip_Flop d_ff_3 (.D(multiplexer_9_out), .clk(ck), .Q(out_6[2]), .reset(reset));  // open: Qn, preset
  and and_3 (and_3_out, out_6[3], and_2_out);
  Multiplexer multiplexer_10 (.in0(out_6[3]), .in1(xor_3_out), .out(multiplexer_10_out), .sel(inc));
  xor xor_3 (xor_3_out, and_2_out, out_6[3]);
  Multiplexer multiplexer_11 (.in0(multiplexer_10_out), .in1(in_1[3]), .out(multiplexer_11_out), .sel(load));
  Multiplexer multiplexer_12 (.in0(multiplexer_11_out), .in1(1'b0), .out(multiplexer_12_out), .sel(reset));
  D_Flip_Flop d_ff_4 (.D(multiplexer_12_out), .clk(ck), .Q(out_6[3]), .reset(reset));  // open: Qn, preset
  and and_4 (and_4_out, out_6[4], and_3_out);
  xor xor_4 (xor_4_out, and_3_out, out_6[4]);
  Multiplexer multiplexer_13 (.in0(out_6[4]), .in1(xor_4_out), .out(multiplexer_13_out), .sel(inc));
  Multiplexer multiplexer_14 (.in0(multiplexer_13_out), .in1(in_1[4]), .out(multiplexer_14_out), .sel(load));
  D_Flip_Flop d_ff_5 (.D(multiplexer_15_out), .clk(ck), .Q(out_6[4]), .reset(reset));  // open: Qn, preset
  Multiplexer multiplexer_15 (.in0(multiplexer_14_out), .in1(1'b0), .out(multiplexer_15_out), .sel(reset));
  and and_5 (and_5_out, out_6[5], and_4_out);
  xor xor_5 (xor_5_out, and_4_out, out_6[5]);
  Multiplexer multiplexer_16 (.in0(out_6[5]), .in1(xor_5_out), .out(multiplexer_16_out), .sel(inc));
  Multiplexer multiplexer_17 (.in0(multiplexer_16_out), .in1(in_1[5]), .out(multiplexer_17_out), .sel(load));
  D_Flip_Flop d_ff_6 (.D(multiplexer_18_out), .clk(ck), .Q(out_6[5]), .reset(reset));  // open: Qn, preset
  Multiplexer multiplexer_18 (.in0(multiplexer_17_out), .in1(1'b0), .out(multiplexer_18_out), .sel(reset));
  and and_6 (and_6_out, out_6[6], and_5_out);
  xor xor_6 (xor_6_out, and_5_out, out_6[6]);
  Multiplexer multiplexer_19 (.in0(out_6[6]), .in1(xor_6_out), .out(multiplexer_19_out), .sel(inc));
  Multiplexer multiplexer_20 (.in0(multiplexer_19_out), .in1(in_1[6]), .out(multiplexer_20_out), .sel(load));
  D_Flip_Flop d_ff_7 (.D(multiplexer_21_out), .clk(ck), .Q(out_6[6]), .reset(reset));  // open: Qn, preset
  Multiplexer multiplexer_21 (.in0(multiplexer_20_out), .in1(1'b0), .out(multiplexer_21_out), .sel(reset));
  and and_7 (and_7_out, out_6[7], and_6_out);
  xor xor_7 (xor_7_out, and_6_out, out_6[7]);
  Multiplexer multiplexer_22 (.in0(out_6[7]), .in1(xor_7_out), .out(multiplexer_22_out), .sel(inc));
  Multiplexer multiplexer_23 (.in0(multiplexer_22_out), .in1(in_1[7]), .out(multiplexer_23_out), .sel(load));
  D_Flip_Flop d_ff_8 (.D(multiplexer_24_out), .clk(ck), .Q(out_6[7]), .reset(reset));  // open: Qn, preset
  Multiplexer multiplexer_24 (.in0(multiplexer_23_out), .in1(1'b0), .out(multiplexer_24_out), .sel(reset));
  and and_8 (and_8_out, out_6[8], and_7_out);
  Multiplexer multiplexer_25 (.in0(out_6[8]), .in1(xor_8_out), .out(multiplexer_25_out), .sel(inc));
  xor xor_8 (xor_8_out, and_7_out, out_6[8]);
  Multiplexer multiplexer_26 (.in0(multiplexer_25_out), .in1(in_1[8]), .out(multiplexer_26_out), .sel(load));
  D_Flip_Flop d_ff_9 (.D(multiplexer_27_out), .clk(ck), .Q(out_6[8]), .reset(reset));  // open: Qn, preset
  Multiplexer multiplexer_27 (.in0(multiplexer_26_out), .in1(1'b0), .out(multiplexer_27_out), .sel(reset));
  and and_9 (and_9_out, out_6[9], and_8_out);
  Multiplexer multiplexer_28 (.in0(out_6[9]), .in1(xor_9_out), .out(multiplexer_28_out), .sel(inc));
  xor xor_9 (xor_9_out, and_8_out, out_6[9]);
  Multiplexer multiplexer_29 (.in0(multiplexer_28_out), .in1(in_1[9]), .out(multiplexer_29_out), .sel(load));
  D_Flip_Flop d_ff_10 (.D(multiplexer_30_out), .clk(ck), .Q(out_6[9]), .reset(reset));  // open: Qn, preset
  Multiplexer multiplexer_30 (.in0(multiplexer_29_out), .in1(1'b0), .out(multiplexer_30_out), .sel(reset));
  and and_10 (and_10_out, out_6[10], and_9_out);
  Multiplexer multiplexer_31 (.in0(out_6[10]), .in1(xor_10_out), .out(multiplexer_31_out), .sel(inc));
  xor xor_10 (xor_10_out, and_9_out, out_6[10]);
  Multiplexer multiplexer_32 (.in0(multiplexer_31_out), .in1(in_1[10]), .out(multiplexer_32_out), .sel(load));
  Multiplexer multiplexer_33 (.in0(multiplexer_32_out), .in1(1'b0), .out(multiplexer_33_out), .sel(reset));
  D_Flip_Flop d_ff_11 (.D(multiplexer_33_out), .clk(ck), .Q(out_6[10]), .reset(reset));  // open: Qn, preset
  and and_11 (and_11_out, out_6[11], and_10_out);
  Multiplexer multiplexer_34 (.in0(out_6[11]), .in1(xor_11_out), .out(multiplexer_34_out), .sel(inc));
  xor xor_11 (xor_11_out, and_10_out, out_6[11]);
  Multiplexer multiplexer_35 (.in0(multiplexer_34_out), .in1(in_1[11]), .out(multiplexer_35_out), .sel(load));
  Multiplexer multiplexer_36 (.in0(multiplexer_35_out), .in1(1'b0), .out(multiplexer_36_out), .sel(reset));
  D_Flip_Flop d_ff_12 (.D(multiplexer_36_out), .clk(ck), .Q(out_6[11]), .reset(reset));  // open: Qn, preset
  and and_12 (and_12_out, out_6[12], and_11_out);
  xor xor_12 (xor_12_out, and_11_out, out_6[12]);
  Multiplexer multiplexer_37 (.in0(out_6[12]), .in1(xor_12_out), .out(multiplexer_37_out), .sel(inc));
  Multiplexer multiplexer_38 (.in0(multiplexer_37_out), .in1(in_1[12]), .out(multiplexer_38_out), .sel(load));
  D_Flip_Flop d_ff_13 (.D(multiplexer_39_out), .clk(ck), .Q(out_6[12]), .reset(reset));  // open: Qn, preset
  Multiplexer multiplexer_39 (.in0(multiplexer_38_out), .in1(1'b0), .out(multiplexer_39_out), .sel(reset));
  and and_13 (and_13_out, out_6[13], and_12_out);
  xor xor_13 (xor_13_out, and_12_out, out_6[13]);
  Multiplexer multiplexer_40 (.in0(out_6[13]), .in1(xor_13_out), .out(multiplexer_40_out), .sel(inc));
  Multiplexer multiplexer_41 (.in0(multiplexer_40_out), .in1(in_1[13]), .out(multiplexer_41_out), .sel(load));
  D_Flip_Flop d_ff_14 (.D(multiplexer_42_out), .clk(ck), .Q(out_6[13]), .reset(reset));  // open: Qn, preset
  Multiplexer multiplexer_42 (.in0(multiplexer_41_out), .in1(1'b0), .out(multiplexer_42_out), .sel(reset));
  and and_14 (and_14_out, out_6[14], and_13_out);
  xor xor_14 (xor_14_out, and_13_out, out_6[14]);
  Multiplexer multiplexer_43 (.in0(out_6[14]), .in1(xor_14_out), .out(multiplexer_43_out), .sel(inc));
  Multiplexer multiplexer_44 (.in0(multiplexer_43_out), .in1(in_1[14]), .out(multiplexer_44_out), .sel(load));
  D_Flip_Flop d_ff_15 (.D(multiplexer_45_out), .clk(ck), .Q(out_6[14]), .reset(reset));  // open: Qn, preset
  Multiplexer multiplexer_45 (.in0(multiplexer_44_out), .in1(1'b0), .out(multiplexer_45_out), .sel(reset));
  Multiplexer multiplexer_46 (.in0(out_6[15]), .in1(xor_15_out), .out(multiplexer_46_out), .sel(inc));
  xor xor_15 (xor_15_out, and_14_out, out_6[15]);
  Multiplexer multiplexer_47 (.in0(multiplexer_46_out), .in1(in_1[15]), .out(multiplexer_47_out), .sel(load));
  Multiplexer multiplexer_48 (.in0(multiplexer_47_out), .in1(1'b0), .out(multiplexer_48_out), .sel(reset));
  D_Flip_Flop d_ff_16 (.D(multiplexer_48_out), .clk(ck), .Q(out_6[15]), .reset(reset));  // open: Qn, preset
endmodule

module ADDER16 (
  input  [15:0] in_1,
  input  [15:0] in_2,
  input  in_3,
  output [15:0] out_4,
  output out_5
);

  wire and_1_out, and_2_out, and_3_out, and_4_out, and_5_out, and_6_out, and_7_out, and_8_out, and_9_out,
       and_10_out, and_11_out, and_12_out, and_13_out, and_14_out, and_15_out, and_16_out, and_17_out,
       and_18_out, and_19_out, and_20_out, and_21_out, and_22_out, and_23_out, and_24_out, and_25_out,
       and_26_out, and_27_out, and_28_out, and_29_out, and_30_out, and_31_out, and_32_out, and_33_out,
       and_34_out, and_35_out, and_36_out, and_37_out, and_38_out, and_39_out, and_40_out, and_41_out,
       and_42_out, and_43_out, and_44_out, and_45_out, and_46_out, and_47_out, and_48_out, and_49_out,
       and_50_out, and_51_out, and_52_out, and_53_out, and_54_out, and_55_out, and_56_out, and_57_out,
       and_58_out, and_59_out, and_60_out, and_61_out, and_62_out, and_63_out, and_64_out, and_65_out,
       and_66_out, and_67_out, and_68_out, and_69_out, and_70_out, and_71_out, and_72_out, and_73_out,
       and_74_out, and_75_out, and_76_out, and_77_out, and_78_out, and_79_out, and_80_out, and_81_out,
       and_82_out, and_83_out, and_84_out, and_85_out, and_86_out, and_87_out, and_88_out, and_89_out,
       and_90_out, and_91_out, and_92_out, and_93_out, and_94_out, and_95_out, and_96_out, and_97_out,
       and_98_out, and_99_out, and_100_out, and_101_out, and_102_out, and_103_out, and_104_out, and_105_out,
       and_106_out, and_107_out, and_108_out, and_109_out, and_110_out, and_111_out, and_112_out,
       and_113_out, and_114_out, and_115_out, and_116_out, and_117_out, and_118_out, and_119_out,
       and_120_out, and_121_out, and_122_out, and_123_out, and_124_out, and_125_out, and_126_out,
       and_127_out, and_128_out, and_129_out, and_130_out, and_131_out, and_132_out, and_133_out,
       and_134_out, and_135_out, and_136_out, and_137_out, and_138_out, and_139_out, and_140_out,
       and_141_out, and_142_out, and_143_out, and_144_out, and_145_out, and_146_out, and_147_out,
       and_148_out, and_149_out, and_150_out, and_151_out, and_152_out, or_2_out, or_3_out, or_4_out,
       or_5_out, or_6_out, or_7_out, or_8_out, or_9_out, or_10_out, or_11_out, or_12_out, or_13_out,
       or_14_out, or_15_out, or_16_out, or_17_out, or_18_out, or_19_out, or_20_out, or_21_out, or_22_out,
       or_23_out, or_24_out, or_25_out, or_26_out, or_27_out, or_28_out, or_29_out, or_30_out, or_31_out,
       or_32_out, xor_1_out, xor_3_out, xor_5_out, xor_7_out, xor_9_out, xor_11_out, xor_13_out, xor_15_out,
       xor_17_out, xor_19_out, xor_21_out, xor_23_out, xor_25_out, xor_27_out, xor_29_out, xor_31_out;

  and and_1 (and_1_out, or_2_out, or_3_out, or_6_out, or_7_out, or_9_out, or_11_out, or_13_out, or_15_out, or_17_out, or_19_out, or_21_out, or_23_out, or_25_out, or_27_out, or_29_out, or_30_out, in_3);
  and and_2 (and_2_out, or_2_out, or_3_out, or_6_out, or_7_out, or_9_out, or_11_out, or_13_out, or_15_out, or_17_out, or_19_out, or_21_out, or_23_out, or_25_out, or_27_out, or_29_out, and_151_out);
  and and_3 (and_3_out, or_2_out, or_3_out, or_6_out, or_7_out, or_9_out, or_11_out, or_13_out, or_15_out, or_17_out, or_19_out, or_21_out, or_23_out, or_25_out, or_27_out, and_150_out);
  and and_4 (and_4_out, or_2_out, or_3_out, or_6_out, or_7_out, or_9_out, or_11_out, or_13_out, or_15_out, or_17_out, or_19_out, or_21_out, or_23_out, or_25_out, and_145_out);
  and and_5 (and_5_out, or_2_out, or_3_out, or_6_out, or_7_out, or_9_out, or_11_out, or_13_out, or_15_out, or_17_out, or_19_out, or_21_out, or_23_out, and_141_out);
  and and_6 (and_6_out, or_2_out, or_3_out, or_6_out, or_7_out, or_9_out, or_11_out, or_13_out, or_15_out, or_17_out, or_19_out, or_21_out, and_138_out);
  and and_7 (and_7_out, or_2_out, or_3_out, or_6_out, or_7_out, or_9_out, or_11_out, or_13_out, or_15_out, or_17_out, or_19_out, and_130_out);
  and and_8 (and_8_out, or_2_out, or_3_out, or_6_out, or_7_out, or_9_out, or_11_out, or_13_out, or_15_out, or_17_out, and_124_out);
  and and_9 (and_9_out, or_2_out, or_3_out, or_6_out, or_7_out, or_9_out, or_11_out, or_13_out, or_15_out, and_115_out);
  and and_10 (and_10_out, or_2_out, or_3_out, or_6_out, or_7_out, or_9_out, or_11_out, or_13_out, and_108_out);
  and and_11 (and_11_out, or_2_out, or_3_out, or_6_out, or_7_out, or_9_out, or_11_out, and_98_out);
  and and_12 (and_12_out, or_2_out, or_3_out, or_6_out, or_7_out, or_9_out, and_85_out);
  and and_13 (and_13_out, or_2_out, or_3_out, or_6_out, or_7_out, and_73_out);
  and and_14 (and_14_out, or_2_out, or_3_out, or_6_out, and_62_out);
  or or_1 (out_5, and_1_out, and_2_out, and_3_out, and_4_out, and_5_out, and_6_out, and_7_out, and_8_out, and_9_out, and_10_out, and_11_out, and_12_out, and_13_out, and_14_out, and_16_out, and_17_out, and_15_out);
  or or_2 (or_2_out, in_1[15], in_2[15]);
  and and_15 (and_15_out, in_1[15], in_2[15]);
  and and_16 (and_16_out, or_2_out, or_3_out, and_46_out);
  and and_17 (and_17_out, or_2_out, and_32_out);
  xor xor_1 (xor_1_out, in_1[15], in_2[15]);
  xor xor_2 (out_4[15], xor_1_out, or_4_out);
  and and_18 (and_18_out, or_3_out, or_6_out, or_7_out, or_9_out, or_11_out, or_13_out, or_15_out, or_17_out, or_19_out, or_21_out, or_23_out, or_25_out, or_27_out, or_29_out, or_30_out, in_3);
  and and_19 (and_19_out, or_3_out, or_6_out, or_7_out, or_9_out, or_11_out, or_13_out, or_15_out, or_17_out, or_19_out, or_21_out, or_23_out, or_25_out, or_27_out, or_29_out, and_151_out);
  and and_20 (and_20_out, or_3_out, or_6_out, or_7_out, or_9_out, or_11_out, or_13_out, or_15_out, or_17_out, or_19_out, or_21_out, or_23_out, or_25_out, or_27_out, and_150_out);
  and and_21 (and_21_out, or_3_out, or_6_out, or_7_out, or_9_out, or_11_out, or_13_out, or_15_out, or_17_out, or_19_out, or_21_out, or_23_out, or_25_out, and_145_out);
  and and_22 (and_22_out, or_3_out, or_6_out, or_7_out, or_9_out, or_11_out, or_13_out, or_15_out, or_17_out, or_19_out, or_21_out, or_23_out, and_141_out);
  and and_23 (and_23_out, or_3_out, or_6_out, or_7_out, or_9_out, or_11_out, or_13_out, or_15_out, or_17_out, or_19_out, or_21_out, and_138_out);
  and and_24 (and_24_out, or_3_out, or_6_out, or_7_out, or_9_out, or_11_out, or_13_out, or_15_out, or_17_out, or_19_out, and_130_out);
  and and_25 (and_25_out, or_3_out, or_6_out, or_7_out, or_9_out, or_11_out, or_13_out, or_15_out, or_17_out, and_124_out);
  and and_26 (and_26_out, or_3_out, or_6_out, or_7_out, or_9_out, or_11_out, or_13_out, or_15_out, and_115_out);
  and and_27 (and_27_out, or_3_out, or_6_out, or_7_out, or_9_out, or_11_out, or_13_out, and_108_out);
  and and_28 (and_28_out, or_3_out, or_6_out, or_7_out, or_9_out, or_11_out, and_98_out);
  and and_29 (and_29_out, or_3_out, or_6_out, or_7_out, or_9_out, and_85_out);
  or or_3 (or_3_out, in_1[14], in_2[14]);
  and and_30 (and_30_out, or_3_out, or_6_out, or_7_out, and_73_out);
  and and_31 (and_31_out, or_3_out, or_6_out, and_62_out);
  or or_4 (or_4_out, and_18_out, and_19_out, and_20_out, and_21_out, and_22_out, and_23_out, and_24_out, and_25_out, and_26_out, and_27_out, and_28_out, and_29_out, and_30_out, and_31_out, and_33_out, and_32_out);
  and and_32 (and_32_out, in_1[14], in_2[14]);
  and and_33 (and_33_out, or_3_out, and_46_out);
  xor xor_3 (xor_3_out, in_1[14], in_2[14]);
  xor xor_4 (out_4[14], xor_3_out, or_5_out);
  and and_34 (and_34_out, or_6_out, or_7_out, or_9_out, or_11_out, or_13_out, or_15_out, or_17_out, or_19_out, or_21_out, or_23_out, or_25_out, or_27_out, or_29_out, or_30_out, in_3);
  and and_35 (and_35_out, or_6_out, or_7_out, or_9_out, or_11_out, or_13_out, or_15_out, or_17_out, or_19_out, or_21_out, or_23_out, or_25_out, or_27_out, or_29_out, and_151_out);
  and and_36 (and_36_out, or_6_out, or_7_out, or_9_out, or_11_out, or_13_out, or_15_out, or_17_out, or_19_out, or_21_out, or_23_out, or_25_out, or_27_out, and_150_out);
  and and_37 (and_37_out, or_6_out, or_7_out, or_9_out, or_11_out, or_13_out, or_15_out, or_17_out, or_19_out, or_21_out, or_23_out, or_25_out, and_145_out);
  and and_38 (and_38_out, or_6_out, or_7_out, or_9_out, or_11_out, or_13_out, or_15_out, or_17_out, or_19_out, or_21_out, or_23_out, and_141_out);
  and and_39 (and_39_out, or_6_out, or_7_out, or_9_out, or_11_out, or_13_out, or_15_out, or_17_out, or_19_out, or_21_out, and_138_out);
  and and_40 (and_40_out, or_6_out, or_7_out, or_9_out, or_11_out, or_13_out, or_15_out, or_17_out, or_19_out, and_130_out);
  and and_41 (and_41_out, or_6_out, or_7_out, or_9_out, or_11_out, or_13_out, or_15_out, or_17_out, and_124_out);
  and and_42 (and_42_out, or_6_out, or_7_out, or_9_out, or_11_out, or_13_out, or_15_out, and_115_out);
  and and_43 (and_43_out, or_6_out, or_7_out, or_9_out, or_11_out, or_13_out, and_108_out);
  and and_44 (and_44_out, or_6_out, or_7_out, or_9_out, or_11_out, and_98_out);
  and and_45 (and_45_out, or_6_out, or_7_out, or_9_out, and_85_out);
  or or_5 (or_5_out, and_34_out, and_35_out, and_36_out, and_37_out, and_38_out, and_39_out, and_40_out, and_41_out, and_42_out, and_43_out, and_44_out, and_45_out, and_47_out, and_48_out, and_46_out);
  or or_6 (or_6_out, in_1[13], in_2[13]);
  and and_46 (and_46_out, in_1[13], in_2[13]);
  and and_47 (and_47_out, or_6_out, or_7_out, and_73_out);
  and and_48 (and_48_out, or_6_out, and_62_out);
  xor xor_5 (xor_5_out, in_1[13], in_2[13]);
  xor xor_6 (out_4[13], xor_5_out, or_8_out);
  and and_49 (and_49_out, or_7_out, or_9_out, or_11_out, or_13_out, or_15_out, or_17_out, or_19_out, or_21_out, or_23_out, or_25_out, or_27_out, or_29_out, or_30_out, in_3);
  and and_50 (and_50_out, or_7_out, or_9_out, or_11_out, or_13_out, or_15_out, or_17_out, or_19_out, or_21_out, or_23_out, or_25_out, or_27_out, or_29_out, and_151_out);
  and and_51 (and_51_out, or_7_out, or_9_out, or_11_out, or_13_out, or_15_out, or_17_out, or_19_out, or_21_out, or_23_out, or_25_out, or_27_out, and_150_out);
  and and_52 (and_52_out, or_7_out, or_9_out, or_11_out, or_13_out, or_15_out, or_17_out, or_19_out, or_21_out, or_23_out, or_25_out, and_145_out);
  and and_53 (and_53_out, or_7_out, or_9_out, or_11_out, or_13_out, or_15_out, or_17_out, or_19_out, or_21_out, or_23_out, and_141_out);
  and and_54 (and_54_out, or_7_out, or_9_out, or_11_out, or_13_out, or_15_out, or_17_out, or_19_out, or_21_out, and_138_out);
  and and_55 (and_55_out, or_7_out, or_9_out, or_11_out, or_13_out, or_15_out, or_17_out, or_19_out, and_130_out);
  and and_56 (and_56_out, or_7_out, or_9_out, or_11_out, or_13_out, or_15_out, or_17_out, and_124_out);
  and and_57 (and_57_out, or_7_out, or_9_out, or_11_out, or_13_out, or_15_out, and_115_out);
  and and_58 (and_58_out, or_7_out, or_9_out, or_11_out, or_13_out, and_108_out);
  or or_7 (or_7_out, in_1[12], in_2[12]);
  and and_59 (and_59_out, or_7_out, or_9_out, or_11_out, and_98_out);
  and and_60 (and_60_out, or_7_out, or_9_out, and_85_out);
  and and_61 (and_61_out, or_7_out, and_73_out);
  or or_8 (or_8_out, and_49_out, and_50_out, and_51_out, and_52_out, and_53_out, and_54_out, and_55_out, and_56_out, and_57_out, and_58_out, and_59_out, and_60_out, and_61_out, and_62_out);
  and and_62 (and_62_out, in_1[12], in_2[12]);
  xor xor_7 (xor_7_out, in_1[12], in_2[12]);
  xor xor_8 (out_4[12], xor_7_out, or_10_out);
  and and_63 (and_63_out, or_9_out, or_11_out, or_13_out, or_15_out, or_17_out, or_19_out, or_21_out, or_23_out, or_25_out, or_27_out, or_29_out, or_30_out, in_3);
  and and_64 (and_64_out, or_9_out, or_11_out, or_13_out, or_15_out, or_17_out, or_19_out, or_21_out, or_23_out, or_25_out, or_27_out, or_29_out, and_151_out);
  and and_65 (and_65_out, or_9_out, or_11_out, or_13_out, or_15_out, or_17_out, or_19_out, or_21_out, or_23_out, or_25_out, or_27_out, and_150_out);
  and and_66 (and_66_out, or_9_out, or_11_out, or_13_out, or_15_out, or_17_out, or_19_out, or_21_out, or_23_out, or_25_out, and_145_out);
  and and_67 (and_67_out, or_9_out, or_11_out, or_13_out, or_15_out, or_17_out, or_19_out, or_21_out, or_23_out, and_141_out);
  and and_68 (and_68_out, or_9_out, or_11_out, or_13_out, or_15_out, or_17_out, or_19_out, or_21_out, and_138_out);
  and and_69 (and_69_out, or_9_out, or_11_out, or_13_out, or_15_out, or_17_out, or_19_out, and_130_out);
  and and_70 (and_70_out, or_9_out, or_11_out, or_13_out, or_15_out, or_17_out, and_124_out);
  and and_71 (and_71_out, or_9_out, or_11_out, or_13_out, or_15_out, and_115_out);
  and and_72 (and_72_out, or_9_out, or_11_out, or_13_out, and_108_out);
  or or_9 (or_9_out, in_1[11], in_2[11]);
  and and_73 (and_73_out, in_1[11], in_2[11]);
  and and_74 (and_74_out, or_9_out, or_11_out, and_98_out);
  and and_75 (and_75_out, or_9_out, and_85_out);
  or or_10 (or_10_out, and_63_out, and_64_out, and_65_out, and_66_out, and_67_out, and_68_out, and_69_out, and_70_out, and_71_out, and_72_out, and_74_out, and_75_out, and_73_out);
  xor xor_9 (xor_9_out, in_1[11], in_2[11]);
  xor xor_10 (out_4[11], xor_9_out, or_12_out);
  and and_76 (and_76_out, or_11_out, or_13_out, or_15_out, or_17_out, or_19_out, or_21_out, or_23_out, or_25_out, or_27_out, or_29_out, or_30_out, in_3);
  and and_77 (and_77_out, or_11_out, or_13_out, or_15_out, or_17_out, or_19_out, or_21_out, or_23_out, or_25_out, or_27_out, or_29_out, and_151_out);
  and and_78 (and_78_out, or_11_out, or_13_out, or_15_out, or_17_out, or_19_out, or_21_out, or_23_out, or_25_out, or_27_out, and_150_out);
  and and_79 (and_79_out, or_11_out, or_13_out, or_15_out, or_17_out, or_19_out, or_21_out, or_23_out, or_25_out, and_145_out);
  and and_80 (and_80_out, or_11_out, or_13_out, or_15_out, or_17_out, or_19_out, or_21_out, or_23_out, and_141_out);
  and and_81 (and_81_out, or_11_out, or_13_out, or_15_out, or_17_out, or_19_out, or_21_out, and_138_out);
  and and_82 (and_82_out, or_11_out, or_13_out, or_15_out, or_17_out, or_19_out, and_130_out);
  and and_83 (and_83_out, or_11_out, or_13_out, or_15_out, or_17_out, and_124_out);
  and and_84 (and_84_out, or_11_out, or_13_out, or_15_out, and_115_out);
  or or_11 (or_11_out, in_1[10], in_2[10]);
  and and_85 (and_85_out, in_1[10], in_2[10]);
  and and_86 (and_86_out, or_11_out, or_13_out, and_108_out);
  and and_87 (and_87_out, or_11_out, and_98_out);
  or or_12 (or_12_out, and_76_out, and_77_out, and_78_out, and_79_out, and_80_out, and_81_out, and_82_out, and_83_out, and_84_out, and_86_out, and_87_out, and_85_out);
  xor xor_11 (xor_11_out, in_1[10], in_2[10]);
  xor xor_12 (out_4[10], xor_11_out, or_14_out);
  and and_88 (and_88_out, or_13_out, or_15_out, or_17_out, or_19_out, or_21_out, or_23_out, or_25_out, or_27_out, or_29_out, or_30_out, in_3);
  and and_89 (and_89_out, or_13_out, or_15_out, or_17_out, or_19_out, or_21_out, or_23_out, or_25_out, or_27_out, or_29_out, and_151_out);
  and and_90 (and_90_out, or_13_out, or_15_out, or_17_out, or_19_out, or_21_out, or_23_out, or_25_out, or_27_out, and_150_out);
  and and_91 (and_91_out, or_13_out, or_15_out, or_17_out, or_19_out, or_21_out, or_23_out, or_25_out, and_145_out);
  and and_92 (and_92_out, or_13_out, or_15_out, or_17_out, or_19_out, or_21_out, or_23_out, and_141_out);
  and and_93 (and_93_out, or_13_out, or_15_out, or_17_out, or_19_out, or_21_out, and_138_out);
  and and_94 (and_94_out, or_13_out, or_15_out, or_17_out, or_19_out, and_130_out);
  or or_13 (or_13_out, in_1[9], in_2[9]);
  and and_95 (and_95_out, or_13_out, or_15_out, or_17_out, and_124_out);
  and and_96 (and_96_out, or_13_out, or_15_out, and_115_out);
  and and_97 (and_97_out, or_13_out, and_108_out);
  or or_14 (or_14_out, and_88_out, and_89_out, and_90_out, and_91_out, and_92_out, and_93_out, and_94_out, and_95_out, and_96_out, and_97_out, and_98_out);
  and and_98 (and_98_out, in_1[9], in_2[9]);
  xor xor_13 (xor_13_out, in_1[9], in_2[9]);
  xor xor_14 (out_4[9], xor_13_out, or_16_out);
  and and_99 (and_99_out, or_15_out, or_17_out, or_19_out, or_21_out, or_23_out, or_25_out, or_27_out, or_29_out, or_30_out, in_3);
  and and_100 (and_100_out, or_15_out, or_17_out, or_19_out, or_21_out, or_23_out, or_25_out, or_27_out, or_29_out, and_151_out);
  and and_101 (and_101_out, or_15_out, or_17_out, or_19_out, or_21_out, or_23_out, or_25_out, or_27_out, and_150_out);
  and and_102 (and_102_out, or_15_out, or_17_out, or_19_out, or_21_out, or_23_out, or_25_out, and_145_out);
  and and_103 (and_103_out, or_15_out, or_17_out, or_19_out, or_21_out, or_23_out, and_141_out);
  and and_104 (and_104_out, or_15_out, or_17_out, or_19_out, or_21_out, and_138_out);
  or or_15 (or_15_out, in_1[8], in_2[8]);
  and and_105 (and_105_out, or_15_out, or_17_out, or_19_out, and_130_out);
  and and_106 (and_106_out, or_15_out, or_17_out, and_124_out);
  and and_107 (and_107_out, or_15_out, and_115_out);
  or or_16 (or_16_out, and_99_out, and_100_out, and_101_out, and_102_out, and_103_out, and_104_out, and_105_out, and_106_out, and_107_out, and_108_out);
  and and_108 (and_108_out, in_1[8], in_2[8]);
  xor xor_15 (xor_15_out, in_1[8], in_2[8]);
  xor xor_16 (out_4[8], xor_15_out, or_18_out);
  and and_109 (and_109_out, or_17_out, or_19_out, or_21_out, or_23_out, or_25_out, or_27_out, or_29_out, or_30_out, in_3);
  and and_110 (and_110_out, or_17_out, or_19_out, or_21_out, or_23_out, or_25_out, or_27_out, or_29_out, and_151_out);
  and and_111 (and_111_out, or_17_out, or_19_out, or_21_out, or_23_out, or_25_out, or_27_out, and_150_out);
  and and_112 (and_112_out, or_17_out, or_19_out, or_21_out, or_23_out, or_25_out, and_145_out);
  and and_113 (and_113_out, or_17_out, or_19_out, or_21_out, or_23_out, and_141_out);
  and and_114 (and_114_out, or_17_out, or_19_out, or_21_out, and_138_out);
  or or_17 (or_17_out, in_1[7], in_2[7]);
  and and_115 (and_115_out, in_1[7], in_2[7]);
  and and_116 (and_116_out, or_17_out, or_19_out, and_130_out);
  and and_117 (and_117_out, or_17_out, and_124_out);
  or or_18 (or_18_out, and_109_out, and_110_out, and_111_out, and_112_out, and_113_out, and_114_out, and_116_out, and_117_out, and_115_out);
  and and_118 (and_118_out, or_19_out, or_21_out, or_23_out, or_25_out, or_27_out, or_29_out, or_30_out, in_3);
  xor xor_17 (xor_17_out, in_1[7], in_2[7]);
  xor xor_18 (out_4[7], xor_17_out, or_20_out);
  and and_119 (and_119_out, or_19_out, or_21_out, or_23_out, or_25_out, or_27_out, or_29_out, and_151_out);
  and and_120 (and_120_out, or_19_out, or_21_out, or_23_out, or_25_out, or_27_out, and_150_out);
  and and_121 (and_121_out, or_19_out, or_21_out, or_23_out, or_25_out, and_145_out);
  or or_19 (or_19_out, in_1[6], in_2[6]);
  and and_122 (and_122_out, or_19_out, or_21_out, or_23_out, and_141_out);
  and and_123 (and_123_out, or_19_out, or_21_out, and_138_out);
  or or_20 (or_20_out, and_118_out, and_119_out, and_120_out, and_121_out, and_122_out, and_123_out, and_125_out, and_124_out);
  and and_124 (and_124_out, in_1[6], in_2[6]);
  and and_125 (and_125_out, or_19_out, and_130_out);
  xor xor_19 (xor_19_out, in_1[6], in_2[6]);
  xor xor_20 (out_4[6], xor_19_out, or_22_out);
  and and_126 (and_126_out, or_21_out, or_23_out, or_25_out, or_27_out, or_29_out, or_30_out, in_3);
  and and_127 (and_127_out, or_21_out, or_23_out, or_25_out, or_27_out, or_29_out, and_151_out);
  and and_128 (and_128_out, or_21_out, or_23_out, or_25_out, or_27_out, and_150_out);
  and and_129 (and_129_out, or_21_out, or_23_out, or_25_out, and_145_out);
  or or_21 (or_21_out, in_1[5], in_2[5]);
  and and_130 (and_130_out, in_1[5], in_2[5]);
  and and_131 (and_131_out, or_21_out, or_23_out, and_141_out);
  and and_132 (and_132_out, or_21_out, and_138_out);
  or or_22 (or_22_out, and_126_out, and_127_out, and_128_out, and_129_out, and_131_out, and_132_out, and_130_out);
  and and_133 (and_133_out, or_23_out, or_25_out, or_27_out, or_29_out, or_30_out, in_3);
  xor xor_21 (xor_21_out, in_1[5], in_2[5]);
  xor xor_22 (out_4[5], xor_21_out, or_24_out);
  and and_134 (and_134_out, or_23_out, or_25_out, or_27_out, or_29_out, and_151_out);
  or or_23 (or_23_out, in_1[4], in_2[4]);
  and and_135 (and_135_out, or_23_out, or_25_out, or_27_out, and_150_out);
  and and_136 (and_136_out, or_23_out, or_25_out, and_145_out);
  and and_137 (and_137_out, or_23_out, and_141_out);
  or or_24 (or_24_out, and_133_out, and_134_out, and_135_out, and_136_out, and_137_out, and_138_out);
  and and_138 (and_138_out, in_1[4], in_2[4]);
  xor xor_23 (xor_23_out, in_1[4], in_2[4]);
  xor xor_24 (out_4[4], xor_23_out, or_26_out);
  and and_139 (and_139_out, or_25_out, or_27_out, or_29_out, or_30_out, in_3);
  and and_140 (and_140_out, or_25_out, or_27_out, or_29_out, and_151_out);
  or or_25 (or_25_out, in_1[3], in_2[3]);
  and and_141 (and_141_out, in_1[3], in_2[3]);
  and and_142 (and_142_out, or_25_out, or_27_out, and_150_out);
  and and_143 (and_143_out, or_25_out, and_145_out);
  or or_26 (or_26_out, and_139_out, and_140_out, and_142_out, and_143_out, and_141_out);
  and and_144 (and_144_out, or_27_out, or_29_out, or_30_out, in_3);
  xor xor_25 (xor_25_out, in_1[3], in_2[3]);
  xor xor_26 (out_4[3], xor_25_out, or_28_out);
  or or_27 (or_27_out, in_1[2], in_2[2]);
  and and_145 (and_145_out, in_1[2], in_2[2]);
  and and_146 (and_146_out, or_27_out, or_29_out, and_151_out);
  and and_147 (and_147_out, or_27_out, and_150_out);
  or or_28 (or_28_out, and_144_out, and_146_out, and_147_out, and_145_out);
  or or_29 (or_29_out, in_1[1], in_2[1]);
  and and_148 (and_148_out, or_29_out, or_30_out, in_3);
  and and_149 (and_149_out, or_29_out, and_151_out);
  xor xor_27 (xor_27_out, in_1[2], in_2[2]);
  xor xor_28 (out_4[2], xor_27_out, or_31_out);
  and and_150 (and_150_out, in_1[1], in_2[1]);
  or or_30 (or_30_out, in_1[0], in_2[0]);
  or or_31 (or_31_out, and_148_out, and_149_out, and_150_out);
  xor xor_29 (xor_29_out, in_1[1], in_2[1]);
  xor xor_30 (out_4[1], xor_29_out, or_32_out);
  and and_151 (and_151_out, in_1[0], in_2[0]);
  and and_152 (and_152_out, or_30_out, in_3);
  or or_32 (or_32_out, and_152_out, and_151_out);
  xor xor_31 (xor_31_out, in_1[0], in_2[0]);
  xor xor_32 (out_4[0], xor_31_out, in_3);
endmodule
