// Logisim project MULTI_WAY_GATES.circ as structural Verilog: 7 circuits, main circuit main
module main (
);

  MUX4WAY mux4way_1 ();  // open: in_5, in_2, in_3, in_4, in_1, out_6
  OR8WAY or8way_1 ();  // open: in_1, out_2
  MUX8WAY mux8way_1 ();  // open: in_1, in_2, in_3, in_4, in_5, in_6, in_7, in_8, in_9, out_10
  OR16WAY or16way_1 ();  // open: in_1, out_2
  DMUX8WAY dmux8way_1 ();  // open: in_2, in_1, out_4, out_5, out_6, out_7, out_8, out_9, out_10, out_3
  DMUX4WAY dmux4way_1 ();  // open: in_1, in_2, out_5, out_6, out_3, out_4
endmodule

module MUX4WAY (
  input  in_1,
  input  in_2,
  input  in_3,
  input  in_4,
  input  [1:0] in_5,
  output out_6
);

  wire multiplexer_1_out, multiplexer_2_out;

  Multiplexer multiplexer_1 (.in0(in_1), .in1(in_2), .out(multiplexer_1_out), .sel(in_5[0]));
  Multiplexer multiplexer_2 (.in0(in_3), .in1(in_4), .out(multiplexer_2_out), .sel(in_5[0]));
  Multiplexer multiplexer_3 (.in0(multiplexer_1_out), .in1(multiplexer_2_out), .out(out_6), .sel(in_5[1]));
endmodule

module MUX8WAY (
  input  in_1,
  input  in_2,
  input  in_3,
  input  in_4,
  input  in_5,
  input  in_6,
  input  in_7,
  input  in_8,
  input  [2:0] in_9,
  output out_10
);

  wire mux4way_1_out_6, mux4way_2_out_6;

  MUX4WAY mux4way_1 (.in_5(in_9[1:0]), .in_2(in_2), .in_3(in_3), .in_4(in_4), .in_1(in_1), .out_6(mux4way_1_out_6));
  Multiplexer multiplexer_1 (.in0(mux4way_1_out_6), .in1(mux4way_2_out_6), .out(out_10), .sel(in_9[2]));
  MUX4WAY mux4way_2 (.in_5(in_9[1:0]), .in_2(in_6), .in_3(in_7), .in_4(in_8), .in_1(in_5), .out_6(mux4way_2_out_6));
endmodule

module DMUX4WAY (
  input  in_1,
  input  [1:0] in_2,
  output out_3,
  output out_4,
  output out_5,
  output out_6
);

  wire demultiplexer_1_out0, demultiplexer_1_out1;

  Demultiplexer demultiplexer_1 (.out0(demultiplexer_1_out0), .out1(demultiplexer_1_out1), .in(in_1), .sel(in_2[1]));
  Demultiplexer demultiplexer_2 (.out0(out_3), .out1(out_4), .in(demultiplexer_1_out0), .sel(in_2[0]));
  Demultiplexer demultiplexer_3 (.out0(out_5), .out1(out_6), .in(demultiplexer_1_out1), .sel(in_2[0]));
endmodule

module DMUX8WAY (
  input  in_1,
  input  [2:0] in_2,
  output out_3,
  output out_4,
  output out_5,
  output out_6,
  output out_7,
  output out_8,
  output out_9,
  output out_10
);

  wire demultiplexer_1_out0, demultiplexer_1_out1;

  Demultiplexer demultiplexer_1 (.out0(demultiplexer_1_out0), .out1(demultiplexer_1_out1), .in(in_1), .sel(in_2[2]));
  DMUX4WAY dmux4way_1 (
    .in_1(demultiplexer_1_out0), .in_2(in_2[1:0]), .out_5(out_5), .out_6(out_6), .out_3(out_3), .out_4(out_4));
  DMUX4WAY dmux4way_2 (
    .in_1(demultiplexer_1_out1), .in_2(in_2[1:0]), .out_5(out_9), .out_6(out_10), .out_3(out_7), .out_4(out_8));
endmodule

module OR8WAY (
  input  [7:0] in_1,
  output out_2
);

  wire or_1_out, or_2_out, or_3_out, or_4_out, or_5_out, or_6_out;

  or or_1 (or_1_out, in_1[0], in_1[1]);
  or or_2 (or_2_out, or_1_out, in_1[2]);
  or or_3 (or_3_out, or_2_out, in_1[3]);
  or or_4 (or_4_out, or_3_out, in_1[4]);
  or or_5 (or_5_out, or_4_out, in_1[5]);
  or or_6 (or_6_out, or_5_out, in_1[6]);
  or or_7 (out_2, or_6_out, in_1[7]);
endmodule

module OR16WAY (
  input  [15:0] in_1,
  output out_2
);

  wire or8way_1_out_2, or8way_2_out_2;

  OR8WAY or8way_1 (.in_1(in_1[7:0]), .out_2(or8way_1_out_2));
  or or_1 (out_2, or8way_1_out_2, or8way_2_out_2);
  OR8WAY or8way_2 (.in_1(in_1[15:8]), .out_2(or8way_2_out_2));
endmodule
