// Logisim project PRIMARY_GATES.circ as structural Verilog: 9 circuits, main circuit main
module main (
  input  in_1,
  input  in_2,
  input  in_3,
  input  in_4,
  input  in_5,
  input  in_6,
  input  in_7,
  input  in_8,
  input  in_9,
  input  in_10,
  input  in_11,
  input  in_12,
  input  in_13,
  input  in_14,
  input  in_15,
  input  in_16,
  output out_17,
  output out_18,
  output out_19,
  output out_20,
  output out_21,
  output out_22,
  output out_23,
  output out_24,
  output out_25
);

  HNAND hnand_1 (.in_1(in_2), .in_2(in_3), .out_3(out_17));
  HAND hand_1 (.in_1(in_5), .in_2(in_7), .out_3(out_19));
  MUX mux_1 (.in_1(in_9), .in_2(in_10), .in_3(in_12), .out_4(out_22));
  DMUX dmux_1 (.in_2(in_15), .in_1(in_14), .out_3(out_23), .out_4(out_25));
  HNOT hnot_1 (.in_1(in_6), .out_2(out_20));
  HOR hor_1 (.in_1(in_4), .in_2(in_1), .out_3(out_18));
  HXOR hxor_1 (.in_1(in_8), .in_2(in_11), .out_3(out_21));
  HNOR hnor_1 (.in_1(in_13), .in_2(in_16), .out_3(out_24));
endmodule

module HNAND (
  input  in_1,
  input  in_2,
  output out_3
);

  wire transistor_4_out;

  Transistor transistor_1 (.in(1'b1), .out(out_3), .gate(in_1));
  Transistor transistor_2 (.in(1'b1), .out(out_3), .gate(in_2));
  Transistor #(.\type ("n")) transistor_3 (.in(transistor_4_out), .out(out_3), .gate(in_1));
  Transistor #(.\type ("n")) transistor_4 (.in(1'b0), .out(transistor_4_out), .gate(in_2));
endmodule

module HAND (
  input  in_1,
  input  in_2,
  output out_3
);

  wire hnand_1_out_3;

  HNAND hnand_1 (.in_1(in_1), .in_2(in_2), .out_3(hnand_1_out_3));
  HNAND hnand_2 (.in_1(hnand_1_out_3), .in_2(hnand_1_out_3), .out_3(out_3));
endmodule

module HNOT (
  input  in_1,
  output out_2
);

  HNAND hnand_1 (.in_1(in_1), .in_2(in_1), .out_3(out_2));
endmodule

module HOR (
  input  in_1,
  input  in_2,
  output out_3
);

  wire hnand_1_out_3, hnand_2_out_3;

  HNAND hnand_1 (.in_1(in_1), .in_2(in_1), .out_3(hnand_1_out_3));
  HNAND hnand_2 (.in_1(in_2), .in_2(in_2), .out_3(hnand_2_out_3));
  HNAND hnand_3 (.in_1(hnand_1_out_3), .in_2(hnand_2_out_3), .out_3(out_3));
endmodule

module HXOR (
  input  in_1,
  input  in_2,
  output out_3
);

  wire hand_1_out_3, hnor_1_out_3;

  HAND hand_1 (.in_1(in_1), .in_2(in_2), .out_3(hand_1_out_3));
  HNOR hnor_1 (.in_1(in_1), .in_2(in_2), .out_3(hnor_1_out_3));
  HNOR hnor_2 (.in_1(hand_1_out_3), .in_2(hnor_1_out_3), .out_3(out_3));
endmodule

module HNOR (
  input  in_1,
  input  in_2,
  output out_3
);

  wire hnand_1_out_3, hnand_2_out_3, hnand_3_out_3;

  HNAND hnand_1 (.in_1(in_1), .in_2(in_1), .out_3(hnand_1_out_3));
  HNAND hnand_2 (.in_1(in_2), .in_2(in_2), .out_3(hnand_2_out_3));
  HNAND hnand_3 (.in_1(hnand_1_out_3), .in_2(hnand_2_out_3), .out_3(hnand_3_out_3));
  HNAND hnand_4 (.in_1(hnand_3_out_3), .in_2(hnand_3_out_3), .out_3(out_3));
endmodule

module MUX (
  input  in_1,
  input  in_2,
  input  in_3,
  output out_4
);

  wire hand_1_out_3, hand_2_out_3, hnot_1_out_2;

  HNOT hnot_1 (.in_1(in_3), .out_2(hnot_1_out_2));
  HAND hand_1 (.in_1(hnot_1_out_2), .in_2(in_1), .out_3(hand_1_out_3));
  HAND hand_2 (.in_1(in_3), .in_2(in_2), .out_3(hand_2_out_3));
  HOR hor_1 (.in_1(hand_2_out_3), .in_2(hand_1_out_3), .out_3(out_4));
endmodule

module DMUX (
  input  in_1,
  input  in_2,
  output out_3,
  output out_4
);

  wire hnot_1_out_2;

  HNOT hnot_1 (.in_1(in_2), .out_2(hnot_1_out_2));
  HAND hand_1 (.in_1(hnot_1_out_2), .in_2(in_1), .out_3(out_3));
  HAND hand_2 (.in_1(in_2), .in_2(in_1), .out_3(out_4));
endmodule
