// Logisim project FLIP_FLOP.circ as structural Verilog: 2 circuits, main circuit main
module main (
);

  DFLIP_FLOP dflip_flop_1 ();  // open: in_1, in_2, out_3
endmodule

module DFLIP_FLOP (
  input  in_1,
  input  in_2,
  output out_3
);

  wire nand_1_out, nand_2_out, nand_3_out, nand_4_out, nand_6_out;

  nand nand_1 (nand_1_out, nand_4_out, nand_2_out);
  nand nand_2 (nand_2_out, nand_1_out, in_1);
  nand nand_3 (nand_3_out, nand_2_out, in_1, nand_4_out);
  nand nand_4 (nand_4_out, nand_3_out, in_2);
  nand nand_5 (out_3, nand_2_out, nand_6_out);
  nand nand_6 (nand_6_out, out_3, nand_3_out);
endmodule
