// Logisim project MEMO.circ as structural Verilog: 4 circuits, main circuit main
module main (
  input  in_1,
  input  [7:0] in_2,
  input  in_3,
  input  [15:0] in_4,
  input  in_5,
  output [15:0] out_6
);

  Memo1kB memo1kb_1 (.in_1(in_3), .in_2(in_1), .in_5(in_5), .in_4(in_4), .in_3(in_2), .out_6(out_6));
endmodule

module Memo2byte (
  input  [15:0] in_1,
  input  in_2,
  input  in_3,
  output [15:0] out_4
);

  wire multiplexer_1_out;

  D_Flip_Flop d_ff_1 (.D(in_1[15]), .clk(multiplexer_1_out), .Q(out_4[15]));  // open: Qn, preset, reset
  Multiplexer multiplexer_1 (.in0(1'b0), .in1(in_2), .out(multiplexer_1_out), .sel(in_3));
  D_Flip_Flop d_ff_2 (.D(in_1[14]), .clk(multiplexer_1_out), .Q(out_4[14]));  // open: Qn, preset, reset
  D_Flip_Flop d_ff_3 (.D(in_1[13]), .clk(multiplexer_1_out), .Q(out_4[13]));  // open: Qn, preset, reset
  D_Flip_Flop d_ff_4 (.D(in_1[12]), .clk(multiplexer_1_out), .Q(out_4[12]));  // open: Qn, preset, reset
  D_Flip_Flop d_ff_5 (.D(in_1[11]), .clk(multiplexer_1_out), .Q(out_4[11]));  // open: Qn, preset, reset
  D_Flip_Flop d_ff_6 (.D(in_1[10]), .clk(multiplexer_1_out), .Q(out_4[10]));  // open: Qn, preset, reset
  D_Flip_Flop d_ff_7 (.D(in_1[9]), .clk(multiplexer_1_out), .Q(out_4[9]));  // open: Qn, preset, reset
  D_Flip_Flop d_ff_8 (.D(in_1[8]), .clk(multiplexer_1_out), .Q(out_4[8]));  // open: Qn, preset, reset
  D_Flip_Flop d_ff_9 (.D(in_1[7]), .clk(multiplexer_1_out), .Q(out_4[7]));  // open: Qn, preset, reset
  D_Flip_Flop d_ff_10 (.D(in_1[6]), .clk(multiplexer_1_out), .Q(out_4[6]));  // open: Qn, preset, reset
  D_Flip_Flop d_ff_11 (.D(in_1[5]), .clk(multiplexer_1_out), .Q(out_4[5]));  // open: Qn, preset, reset
  D_Flip_Flop d_ff_12 (.D(in_1[4]), .clk(multiplexer_1_out), .Q(out_4[4]));  // open: Qn, preset, reset
  D_Flip_Flop d_ff_13 (.D(in_1[3]), .clk(multiplexer_1_out), .Q(out_4[3]));  // open: Qn, preset, reset
  D_Flip_Flop d_ff_14 (.D(in_1[2]), .clk(multiplexer_1_out), .Q(out_4[2]));  // open: Qn, preset, reset
  D_Flip_Flop d_ff_15 (.D(in_1[1]), .clk(multiplexer_1_out), .Q(out_4[1]));  // open: Qn, preset, reset
  D_Flip_Flop d_ff_16 (.D(in_1[0]), .clk(multiplexer_1_out), .Q(out_4[0]));  // open: Qn, preset, reset
endmodule

module Memo128byte (
  input  in_1,
  input  [5:0] in_2,
  input  [15:0] in_3,
  input  in_4,
  input  in_5,
  output [15:0] out_6
);

  wire and_1_out, and_2_out, and_3_out, and_4_out, and_5_out, and_6_out, and_7_out, and_8_out, and_9_out,
       and_10_out, and_11_out, and_12_out, and_13_out, and_14_out, and_15_out, and_16_out, and_17_out,
       and_18_out, and_19_out, and_20_out, and_21_out, and_22_out, and_23_out, and_24_out, and_33_out,
       and_34_out, and_35_out, and_36_out, and_37_out, and_38_out, and_39_out, and_40_out, and_41_out,
       and_42_out, and_43_out, and_44_out, and_45_out, and_46_out, and_47_out, and_48_out, and_49_out,
       and_50_out, and_51_out, and_52_out, and_53_out, and_54_out, and_55_out, and_56_out, and_65_out,
       and_66_out, and_67_out, and_68_out, and_69_out, and_70_out, and_71_out, and_72_out, and_73_out,
       and_74_out, and_75_out, and_76_out, and_77_out, and_78_out, and_79_out, and_80_out, and_81_out,
       and_82_out, and_83_out, and_84_out, and_85_out, and_86_out, and_87_out, and_88_out, and_97_out,
       and_98_out, and_99_out, and_100_out, and_101_out, and_102_out, and_103_out, and_104_out, and_105_out,
       and_106_out, and_107_out, and_108_out, and_109_out, and_110_out, and_111_out, and_112_out,
       and_113_out, and_114_out, and_115_out, and_116_out, and_117_out, and_118_out, and_119_out,
       and_120_out, and_129_out, and_130_out, and_131_out, and_132_out, and_133_out, and_134_out,
       and_135_out, and_136_out, and_137_out, and_138_out, and_139_out, and_140_out, and_141_out,
       and_142_out, and_143_out, and_144_out, and_145_out, and_146_out, and_147_out, and_148_out,
       and_149_out, and_150_out, and_151_out, and_152_out, and_161_out, and_162_out, and_163_out,
       and_164_out, and_165_out, and_166_out, and_167_out, and_168_out, and_169_out, and_170_out,
       and_171_out, and_172_out, and_173_out, and_174_out, and_175_out, and_176_out, and_177_out,
       and_178_out, and_179_out, and_180_out, and_181_out, and_182_out, and_183_out, and_184_out,
       and_193_out, and_194_out, and_195_out, and_196_out, and_197_out, and_198_out, and_199_out,
       and_200_out, and_201_out, and_202_out, and_203_out, and_204_out, and_205_out, and_206_out,
       and_207_out, and_208_out, and_209_out, and_210_out, and_211_out, and_212_out, and_213_out,
       and_214_out, and_215_out, and_216_out, and_225_out, and_226_out, and_227_out, and_228_out,
       and_229_out, and_230_out, and_231_out, and_232_out, and_233_out, and_234_out, and_235_out,
       and_236_out, and_237_out, and_238_out, and_239_out, and_240_out, and_241_out, and_242_out,
       and_243_out, and_244_out, and_245_out, and_246_out, and_247_out, and_248_out, demultiplexer_1_out0,
       demultiplexer_1_out1, demultiplexer_1_out2, demultiplexer_1_out3, demultiplexer_1_out4,
       demultiplexer_1_out5, demultiplexer_1_out6, demultiplexer_1_out7, demultiplexer_2_out0,
       demultiplexer_2_out1, demultiplexer_2_out2, demultiplexer_2_out3, demultiplexer_2_out4,
       demultiplexer_2_out5, demultiplexer_2_out6, demultiplexer_2_out7;
  wire [15:0] and_25_out, and_26_out, and_27_out, and_28_out, and_29_out, and_30_out, and_31_out, and_32_out,
       and_57_out, and_58_out, and_59_out, and_60_out, and_61_out, and_62_out, and_63_out, and_64_out,
       and_89_out, and_90_out, and_91_out, and_92_out, and_93_out, and_94_out, and_95_out, and_96_out,
       and_121_out, and_122_out, and_123_out, and_124_out, and_125_out, and_126_out, and_127_out,
       and_128_out, and_153_out, and_154_out, and_155_out, and_156_out, and_157_out, and_158_out,
       and_159_out, and_160_out, and_185_out, and_186_out, and_187_out, and_188_out, and_189_out,
       and_190_out, and_191_out, and_192_out, and_217_out, and_218_out, and_219_out, and_220_out,
       and_221_out, and_222_out, and_223_out, and_224_out, and_249_out, and_250_out, and_251_out,
       and_252_out, and_253_out, and_254_out, and_255_out, and_256_out, bit_extender_1_out,
       bit_extender_2_out, bit_extender_3_out, bit_extender_4_out, bit_extender_5_out, bit_extender_6_out,
       bit_extender_7_out, bit_extender_8_out, bit_extender_9_out, bit_extender_10_out, bit_extender_11_out,
       bit_extender_12_out, bit_extender_13_out, bit_extender_14_out, bit_extender_15_out,
       bit_extender_16_out, bit_extender_17_out, bit_extender_18_out, bit_extender_19_out,
       bit_extender_20_out, bit_extender_21_out, bit_extender_22_out, bit_extender_23_out,
       bit_extender_24_out, bit_extender_25_out, bit_extender_26_out, bit_extender_27_out,
       bit_extender_28_out, bit_extender_29_out, bit_extender_30_out, bit_extender_31_out,
       bit_extender_32_out, bit_extender_33_out, bit_extender_34_out, bit_extender_35_out,
       bit_extender_36_out, bit_extender_37_out, bit_extender_38_out, bit_extender_39_out,
       bit_extender_40_out, bit_extender_41_out, bit_extender_42_out, bit_extender_43_out,
       bit_extender_44_out, bit_extender_45_out, bit_extender_46_out, bit_extender_47_out,
       bit_extender_48_out, bit_extender_49_out, bit_extender_50_out, bit_extender_51_out,
       bit_extender_52_out, bit_extender_53_out, bit_extender_54_out, bit_extender_55_out,
       bit_extender_56_out, bit_extender_57_out, bit_extender_58_out, bit_extender_59_out,
       bit_extender_60_out, bit_extender_61_out, bit_extender_62_out, bit_extender_63_out,
       bit_extender_64_out, memo2byte_1_out_4, memo2byte_2_out_4, memo2byte_3_out_4, memo2byte_4_out_4,
       memo2byte_5_out_4, memo2byte_6_out_4, memo2byte_7_out_4, memo2byte_8_out_4, memo2byte_9_out_4,
       memo2byte_10_out_4, memo2byte_11_out_4, memo2byte_12_out_4, memo2byte_13_out_4, memo2byte_14_out_4,
       memo2byte_15_out_4, memo2byte_16_out_4, memo2byte_17_out_4, memo2byte_18_out_4, memo2byte_19_out_4,
       memo2byte_20_out_4, memo2byte_21_out_4, memo2byte_22_out_4, memo2byte_23_out_4, memo2byte_24_out_4,
       memo2byte_25_out_4, memo2byte_26_out_4, memo2byte_27_out_4, memo2byte_28_out_4, memo2byte_29_out_4,
       memo2byte_30_out_4, memo2byte_31_out_4, memo2byte_32_out_4, memo2byte_33_out_4, memo2byte_34_out_4,
       memo2byte_35_out_4, memo2byte_36_out_4, memo2byte_37_out_4, memo2byte_38_out_4, memo2byte_39_out_4,
       memo2byte_40_out_4, memo2byte_41_out_4, memo2byte_42_out_4, memo2byte_43_out_4, memo2byte_44_out_4,
       memo2byte_45_out_4, memo2byte_46_out_4, memo2byte_47_out_4, memo2byte_48_out_4, memo2byte_49_out_4,
       memo2byte_50_out_4, memo2byte_51_out_4, memo2byte_52_out_4, memo2byte_53_out_4, memo2byte_54_out_4,
       memo2byte_55_out_4, memo2byte_56_out_4, memo2byte_57_out_4, memo2byte_58_out_4, memo2byte_59_out_4,
       memo2byte_60_out_4, memo2byte_61_out_4, memo2byte_62_out_4, memo2byte_63_out_4, memo2byte_64_out_4,
       or_1_out, or_2_out, or_3_out, or_4_out, or_5_out, or_6_out, or_7_out;

  Demultiplexer #(.select(3)) demultiplexer_1 (
    .out0(demultiplexer_1_out0), .out1(demultiplexer_1_out1), .out2(demultiplexer_1_out2),
    .out3(demultiplexer_1_out3), .out4(demultiplexer_1_out4), .out5(demultiplexer_1_out5),
    .out6(demultiplexer_1_out6), .out7(demultiplexer_1_out7), .in(in_1), .sel(in_2[5:3]));
  Demultiplexer #(.select(3)) demultiplexer_2 (
    .out0(demultiplexer_2_out0), .out1(demultiplexer_2_out1), .out2(demultiplexer_2_out2),
    .out3(demultiplexer_2_out3), .out4(demultiplexer_2_out4), .out5(demultiplexer_2_out5),
    .out6(demultiplexer_2_out6), .out7(demultiplexer_2_out7), .in(in_1), .sel(in_2[2:0]));
  and and_1 (and_1_out, demultiplexer_1_out0, demultiplexer_2_out0);
  and and_2 (and_2_out, demultiplexer_1_out1, demultiplexer_2_out0);
  and and_3 (and_3_out, demultiplexer_1_out2, demultiplexer_2_out0);
  and and_4 (and_4_out, demultiplexer_1_out3, demultiplexer_2_out0);
  and and_5 (and_5_out, demultiplexer_1_out4, demultiplexer_2_out0);
  and and_6 (and_6_out, demultiplexer_1_out5, demultiplexer_2_out0);
  and and_7 (and_7_out, demultiplexer_1_out6, demultiplexer_2_out0);
  and and_8 (and_8_out, demultiplexer_1_out7, demultiplexer_2_out0);
  and and_9 (and_9_out, and_1_out, in_5);
  Memo2byte memo2byte_1 (.in_2(in_4), .in_1(in_3), .in_3(and_9_out), .out_4(memo2byte_1_out_4));
  and and_10 (and_10_out, ~and_9_out, and_1_out);  // AND_Gate
  and and_11 (and_11_out, and_2_out, in_5);
  Memo2byte memo2byte_2 (.in_2(in_4), .in_1(in_3), .in_3(and_11_out), .out_4(memo2byte_2_out_4));
  and and_12 (and_12_out, ~and_11_out, and_2_out);  // AND_Gate
  and and_13 (and_13_out, and_3_out, in_5);
  Memo2byte memo2byte_3 (.in_2(in_4), .in_1(in_3), .in_3(and_13_out), .out_4(memo2byte_3_out_4));
  and and_14 (and_14_out, ~and_13_out, and_3_out);  // AND_Gate
  and and_15 (and_15_out, and_4_out, in_5);
  Memo2byte memo2byte_4 (.in_2(in_4), .in_1(in_3), .in_3(and_15_out), .out_4(memo2byte_4_out_4));
  and and_16 (and_16_out, ~and_15_out, and_4_out);  // AND_Gate
  and and_17 (and_17_out, and_5_out, in_5);
  Memo2byte memo2byte_5 (.in_2(in_4), .in_1(in_3), .in_3(and_17_out), .out_4(memo2byte_5_out_4));
  and and_18 (and_18_out, ~and_17_out, and_5_out);  // AND_Gate
  and and_19 (and_19_out, and_6_out, in_5);
  Memo2byte memo2byte_6 (.in_2(in_4), .in_1(in_3), .in_3(and_19_out), .out_4(memo2byte_6_out_4));
  and and_20 (and_20_out, ~and_19_out, and_6_out);  // AND_Gate
  and and_21 (and_21_out, and_7_out, in_5);
  Memo2byte memo2byte_7 (.in_2(in_4), .in_1(in_3), .in_3(and_21_out), .out_4(memo2byte_7_out_4));
  and and_22 (and_22_out, ~and_21_out, and_7_out);  // AND_Gate
  and and_23 (and_23_out, and_8_out, in_5);
  Memo2byte memo2byte_8 (.in_2(in_4), .in_1(in_3), .in_3(and_23_out), .out_4(memo2byte_8_out_4));
  and and_24 (and_24_out, ~and_23_out, and_8_out);  // AND_Gate
  assign bit_extender_1_out = {{15{and_10_out}}, and_10_out};  // Bit_Extender bit_extender_1
  assign bit_extender_2_out = {{15{and_12_out}}, and_12_out};  // Bit_Extender bit_extender_2
  assign bit_extender_3_out = {{15{and_14_out}}, and_14_out};  // Bit_Extender bit_extender_3
  assign bit_extender_4_out = {{15{and_16_out}}, and_16_out};  // Bit_Extender bit_extender_4
  assign bit_extender_5_out = {{15{and_18_out}}, and_18_out};  // Bit_Extender bit_extender_5
  assign bit_extender_6_out = {{15{and_20_out}}, and_20_out};  // Bit_Extender bit_extender_6
  assign bit_extender_7_out = {{15{and_22_out}}, and_22_out};  // Bit_Extender bit_extender_7
  assign bit_extender_8_out = {{15{and_24_out}}, and_24_out};  // Bit_Extender bit_extender_8
  assign and_25_out = memo2byte_1_out_4 & bit_extender_1_out;  // AND_Gate and_25, 16 bits wide
  assign and_26_out = memo2byte_2_out_4 & bit_extender_2_out;  // AND_Gate and_26, 16 bits wide
  assign and_27_out = memo2byte_3_out_4 & bit_extender_3_out;  // AND_Gate and_27, 16 bits wide
  assign and_28_out = memo2byte_4_out_4 & bit_extender_4_out;  // AND_Gate and_28, 16 bits wide
  assign and_29_out = memo2byte_5_out_4 & bit_extender_5_out;  // AND_Gate and_29, 16 bits wide
  assign and_30_out = memo2byte_6_out_4 & bit_extender_6_out;  // AND_Gate and_30, 16 bits wide
  assign and_31_out = memo2byte_7_out_4 & bit_extender_7_out;  // AND_Gate and_31, 16 bits wide
  assign and_32_out = memo2byte_8_out_4 & bit_extender_8_out;  // AND_Gate and_32, 16 bits wide
  assign or_1_out = and_25_out | and_26_out | and_27_out | and_28_out | and_29_out | and_30_out | and_31_out | and_32_out;  // OR_Gate or_1, 16 bits wide
  and and_33 (and_33_out, demultiplexer_1_out0, demultiplexer_2_out1);
  and and_34 (and_34_out, and_33_out, in_5);
  and and_35 (and_35_out, demultiplexer_1_out1, demultiplexer_2_out1);
  and and_36 (and_36_out, and_35_out, in_5);
  and and_37 (and_37_out, demultiplexer_1_out2, demultiplexer_2_out1);
  and and_38 (and_38_out, and_37_out, in_5);
  and and_39 (and_39_out, demultiplexer_1_out3, demultiplexer_2_out1);
  and and_40 (and_40_out, and_39_out, in_5);
  and and_41 (and_41_out, demultiplexer_1_out4, demultiplexer_2_out1);
  and and_42 (and_42_out, and_41_out, in_5);
  and and_43 (and_43_out, demultiplexer_1_out5, demultiplexer_2_out1);
  and and_44 (and_44_out, and_43_out, in_5);
  and and_45 (and_45_out, demultiplexer_1_out6, demultiplexer_2_out1);
  and and_46 (and_46_out, and_45_out, in_5);
  and and_47 (and_47_out, demultiplexer_1_out7, demultiplexer_2_out1);
  and and_48 (and_48_out, and_47_out, in_5);
  Memo2byte memo2byte_9 (.in_2(in_4), .in_1(in_3), .in_3(and_34_out), .out_4(memo2byte_9_out_4));
  and and_49 (and_49_out, ~and_34_out, and_33_out);  // AND_Gate
  Memo2byte memo2byte_10 (.in_2(in_4), .in_1(in_3), .in_3(and_36_out), .out_4(memo2byte_10_out_4));
  and and_50 (and_50_out, ~and_36_out, and_35_out);  // AND_Gate
  Memo2byte memo2byte_11 (.in_2(in_4), .in_1(in_3), .in_3(and_38_out), .out_4(memo2byte_11_out_4));
  and and_51 (and_51_out, ~and_38_out, and_37_out);  // AND_Gate
  Memo2byte memo2byte_12 (.in_2(in_4), .in_1(in_3), .in_3(and_40_out), .out_4(memo2byte_12_out_4));
  and and_52 (and_52_out, ~and_40_out, and_39_out);  // AND_Gate
  Memo2byte memo2byte_13 (.in_2(in_4), .in_1(in_3), .in_3(and_42_out), .out_4(memo2byte_13_out_4));
  and and_53 (and_53_out, ~and_42_out, and_41_out);  // AND_Gate
  Memo2byte memo2byte_14 (.in_2(in_4), .in_1(in_3), .in_3(and_44_out), .out_4(memo2byte_14_out_4));
  and and_54 (and_54_out, ~and_44_out, and_43_out);  // AND_Gate
  Memo2byte memo2byte_15 (.in_2(in_4), .in_1(in_3), .in_3(and_46_out), .out_4(memo2byte_15_out_4));
  and and_55 (and_55_out, ~and_46_out, and_45_out);  // AND_Gate
  Memo2byte memo2byte_16 (.in_2(in_4), .in_1(in_3), .in_3(and_48_out), .out_4(memo2byte_16_out_4));
  and and_56 (and_56_out, ~and_48_out, and_47_out);  // AND_Gate
  assign and_57_out = memo2byte_9_out_4 & bit_extender_9_out;  // AND_Gate and_57, 16 bits wide
  assign bit_extender_9_out = {{15{and_49_out}}, and_49_out};  // Bit_Extender bit_extender_9
  assign and_58_out = memo2byte_10_out_4 & bit_extender_10_out;  // AND_Gate and_58, 16 bits wide
  assign bit_extender_10_out = {{15{and_50_out}}, and_50_out};  // Bit_Extender bit_extender_10
  assign and_59_out = memo2byte_11_out_4 & bit_extender_11_out;  // AND_Gate and_59, 16 bits wide
  assign bit_extender_11_out = {{15{and_51_out}}, and_51_out};  // Bit_Extender bit_extender_11
  assign and_60_out = memo2byte_12_out_4 & bit_extender_12_out;  // AND_Gate and_60, 16 bits wide
  assign bit_extender_12_out = {{15{and_52_out}}, and_52_out};  // Bit_Extender bit_extender_12
  assign and_61_out = memo2byte_13_out_4 & bit_extender_13_out;  // AND_Gate and_61, 16 bits wide
  assign bit_extender_13_out = {{15{and_53_out}}, and_53_out};  // Bit_Extender bit_extender_13
  assign and_62_out = memo2byte_14_out_4 & bit_extender_14_out;  // AND_Gate and_62, 16 bits wide
  assign bit_extender_14_out = {{15{and_54_out}}, and_54_out};  // Bit_Extender bit_extender_14
  assign and_63_out = memo2byte_15_out_4 & bit_extender_15_out;  // AND_Gate and_63, 16 bits wide
  assign bit_extender_15_out = {{15{and_55_out}}, and_55_out};  // Bit_Extender bit_extender_15
  assign and_64_out = memo2byte_16_out_4 & bit_extender_16_out;  // AND_Gate and_64, 16 bits wide
  assign bit_extender_16_out = {{15{and_56_out}}, and_56_out};  // Bit_Extender bit_extender_16
  and and_65 (and_65_out, demultiplexer_1_out0, demultiplexer_2_out2);
  and and_66 (and_66_out, demultiplexer_1_out1, demultiplexer_2_out2);
  and and_67 (and_67_out, demultiplexer_1_out2, demultiplexer_2_out2);
  and and_68 (and_68_out, demultiplexer_1_out3, demultiplexer_2_out2);
  and and_69 (and_69_out, demultiplexer_1_out4, demultiplexer_2_out2);
  and and_70 (and_70_out, demultiplexer_1_out5, demultiplexer_2_out2);
  and and_71 (and_71_out, demultiplexer_1_out6, demultiplexer_2_out2);
  and and_72 (and_72_out, demultiplexer_1_out7, demultiplexer_2_out2);
  assign or_2_out = and_57_out | and_58_out | and_59_out | and_60_out | or_1_out | and_61_out | and_62_out | and_63_out | and_64_out;  // OR_Gate or_2, 16 bits wide
  buf and_73 (and_73_out, in_5);  // AND_Gate
  and and_74 (and_74_out, and_66_out, in_5);
  buf and_75 (and_75_out, in_5);  // AND_Gate
  and and_76 (and_76_out, and_68_out, in_5);
  buf and_77 (and_77_out, in_5);  // AND_Gate
  and and_78 (and_78_out, and_70_out, in_5);
  buf and_79 (and_79_out, in_5);  // AND_Gate
  and and_80 (and_80_out, and_72_out, in_5);
  Memo2byte memo2byte_17 (.in_2(in_4), .in_1(in_3), .in_3(and_73_out), .out_4(memo2byte_17_out_4));
  assign bit_extender_17_out = {{15{and_81_out}}, and_81_out};  // Bit_Extender bit_extender_17
  and and_81 (and_81_out, ~and_73_out, and_65_out);  // AND_Gate
  Memo2byte memo2byte_18 (.in_2(in_4), .in_1(in_3), .in_3(and_74_out), .out_4(memo2byte_18_out_4));
  assign bit_extender_18_out = {{15{and_82_out}}, and_82_out};  // Bit_Extender bit_extender_18
  and and_82 (and_82_out, ~and_74_out, and_66_out);  // AND_Gate
  Memo2byte memo2byte_19 (.in_2(in_4), .in_1(in_3), .in_3(and_75_out), .out_4(memo2byte_19_out_4));
  assign bit_extender_19_out = {{15{and_83_out}}, and_83_out};  // Bit_Extender bit_extender_19
  and and_83 (and_83_out, ~and_75_out, and_67_out);  // AND_Gate
  Memo2byte memo2byte_20 (.in_2(in_4), .in_1(in_3), .in_3(and_76_out), .out_4(memo2byte_20_out_4));
  assign bit_extender_20_out = {{15{and_84_out}}, and_84_out};  // Bit_Extender bit_extender_20
  and and_84 (and_84_out, ~and_76_out, and_68_out);  // AND_Gate
  Memo2byte memo2byte_21 (.in_2(in_4), .in_1(in_3), .in_3(and_77_out), .out_4(memo2byte_21_out_4));
  assign bit_extender_21_out = {{15{and_85_out}}, and_85_out};  // Bit_Extender bit_extender_21
  and and_85 (and_85_out, ~and_77_out, and_69_out);  // AND_Gate
  Memo2byte memo2byte_22 (.in_2(in_4), .in_1(in_3), .in_3(and_78_out), .out_4(memo2byte_22_out_4));
  assign bit_extender_22_out = {{15{and_86_out}}, and_86_out};  // Bit_Extender bit_extender_22
  and and_86 (and_86_out, ~and_78_out, and_70_out);  // AND_Gate
  Memo2byte memo2byte_23 (.in_2(in_4), .in_1(in_3), .in_3(and_79_out), .out_4(memo2byte_23_out_4));
  assign bit_extender_23_out = {{15{and_87_out}}, and_87_out};  // Bit_Extender bit_extender_23
  and and_87 (and_87_out, ~and_79_out, and_71_out);  // AND_Gate
  Memo2byte memo2byte_24 (.in_2(in_4), .in_1(in_3), .in_3(and_80_out), .out_4(memo2byte_24_out_4));
  assign bit_extender_24_out = {{15{and_88_out}}, and_88_out};  // Bit_Extender bit_extender_24
  and and_88 (and_88_out, ~and_80_out, and_72_out);  // AND_Gate
  assign and_89_out = memo2byte_17_out_4 & bit_extender_17_out;  // AND_Gate and_89, 16 bits wide
  assign and_90_out = memo2byte_18_out_4 & bit_extender_18_out;  // AND_Gate and_90, 16 bits wide
  assign and_91_out = memo2byte_19_out_4 & bit_extender_19_out;  // AND_Gate and_91, 16 bits wide
  assign and_92_out = memo2byte_20_out_4 & bit_extender_20_out;  // AND_Gate and_92, 16 bits wide
  assign and_93_out = memo2byte_21_out_4 & bit_extender_21_out;  // AND_Gate and_93, 16 bits wide
  assign and_94_out = memo2byte_22_out_4 & bit_extender_22_out;  // AND_Gate and_94, 16 bits wide
  assign and_95_out = memo2byte_23_out_4 & bit_extender_23_out;  // AND_Gate and_95, 16 bits wide
  assign and_96_out = memo2byte_24_out_4 & bit_extender_24_out;  // AND_Gate and_96, 16 bits wide
  and and_97 (and_97_out, demultiplexer_1_out0, demultiplexer_2_out3);
  and and_98 (and_98_out, demultiplexer_1_out1, demultiplexer_2_out3);
  and and_99 (and_99_out, demultiplexer_1_out2, demultiplexer_2_out3);
  and and_100 (and_100_out, demultiplexer_1_out3, demultiplexer_2_out3);
  and and_101 (and_101_out, demultiplexer_1_out4, demultiplexer_2_out3);
  and and_102 (and_102_out, demultiplexer_1_out5, demultiplexer_2_out3);
  and and_103 (and_103_out, demultiplexer_1_out6, demultiplexer_2_out3);
  and and_104 (and_104_out, demultiplexer_1_out7, demultiplexer_2_out3);
  assign or_3_out = and_89_out | and_90_out | and_91_out | and_92_out | or_2_out | and_93_out | and_94_out | and_95_out | and_96_out;  // OR_Gate or_3, 16 bits wide
  buf and_105 (and_105_out, in_5);  // AND_Gate
  Memo2byte memo2byte_25 (.in_2(in_4), .in_1(in_3), .in_3(and_105_out), .out_4(memo2byte_25_out_4));
  and and_106 (and_106_out, and_98_out, in_5);
  Memo2byte memo2byte_26 (.in_2(in_4), .in_1(in_3), .in_3(and_106_out), .out_4(memo2byte_26_out_4));
  buf and_107 (and_107_out, in_5);  // AND_Gate
  Memo2byte memo2byte_27 (.in_2(in_4), .in_1(in_3), .in_3(and_107_out), .out_4(memo2byte_27_out_4));
  and and_108 (and_108_out, and_100_out, in_5);
  Memo2byte memo2byte_28 (.in_2(in_4), .in_1(in_3), .in_3(and_108_out), .out_4(memo2byte_28_out_4));
  buf and_109 (and_109_out, in_5);  // AND_Gate
  Memo2byte memo2byte_29 (.in_2(in_4), .in_1(in_3), .in_3(and_109_out), .out_4(memo2byte_29_out_4));
  and and_110 (and_110_out, and_102_out, in_5);
  Memo2byte memo2byte_30 (.in_2(in_4), .in_1(in_3), .in_3(and_110_out), .out_4(memo2byte_30_out_4));
  buf and_111 (and_111_out, in_5);  // AND_Gate
  Memo2byte memo2byte_31 (.in_2(in_4), .in_1(in_3), .in_3(and_111_out), .out_4(memo2byte_31_out_4));
  and and_112 (and_112_out, and_104_out, in_5);
  Memo2byte memo2byte_32 (.in_2(in_4), .in_1(in_3), .in_3(and_112_out), .out_4(memo2byte_32_out_4));
  assign bit_extender_25_out = {{15{and_113_out}}, and_113_out};  // Bit_Extender bit_extender_25
  and and_113 (and_113_out, ~and_105_out, and_97_out);  // AND_Gate
  assign bit_extender_26_out = {{15{and_114_out}}, and_114_out};  // Bit_Extender bit_extender_26
  and and_114 (and_114_out, ~and_106_out, and_98_out);  // AND_Gate
  assign bit_extender_27_out = {{15{and_115_out}}, and_115_out};  // Bit_Extender bit_extender_27
  and and_115 (and_115_out, ~and_107_out, and_99_out);  // AND_Gate
  assign bit_extender_28_out = {{15{and_116_out}}, and_116_out};  // Bit_Extender bit_extender_28
  and and_116 (and_116_out, ~and_108_out, and_100_out);  // AND_Gate
  assign bit_extender_29_out = {{15{and_117_out}}, and_117_out};  // Bit_Extender bit_extender_29
  and and_117 (and_117_out, ~and_109_out, and_101_out);  // AND_Gate
  assign bit_extender_30_out = {{15{and_118_out}}, and_118_out};  // Bit_Extender bit_extender_30
  and and_118 (and_118_out, ~and_110_out, and_102_out);  // AND_Gate
  assign bit_extender_31_out = {{15{and_119_out}}, and_119_out};  // Bit_Extender bit_extender_31
  and and_119 (and_119_out, ~and_111_out, and_103_out);  // AND_Gate
  assign bit_extender_32_out = {{15{and_120_out}}, and_120_out};  // Bit_Extender bit_extender_32
  and and_120 (and_120_out, ~and_112_out, and_104_out);  // AND_Gate
  assign and_121_out = memo2byte_25_out_4 & bit_extender_25_out;  // AND_Gate and_121, 16 bits wide
  assign and_122_out = memo2byte_26_out_4 & bit_extender_26_out;  // AND_Gate and_122, 16 bits wide
  assign and_123_out = memo2byte_27_out_4 & bit_extender_27_out;  // AND_Gate and_123, 16 bits wide
  assign and_124_out = memo2byte_28_out_4 & bit_extender_28_out;  // AND_Gate and_124, 16 bits wide
  assign and_125_out = memo2byte_29_out_4 & bit_extender_29_out;  // AND_Gate and_125, 16 bits wide
  assign and_126_out = memo2byte_30_out_4 & bit_extender_30_out;  // AND_Gate and_126, 16 bits wide
  assign and_127_out = memo2byte_31_out_4 & bit_extender_31_out;  // AND_Gate and_127, 16 bits wide
  assign and_128_out = memo2byte_32_out_4 & bit_extender_32_out;  // AND_Gate and_128, 16 bits wide
  and and_129 (and_129_out, demultiplexer_1_out0, demultiplexer_2_out4);
  and and_130 (and_130_out, demultiplexer_1_out1, demultiplexer_2_out4);
  and and_131 (and_131_out, demultiplexer_1_out2, demultiplexer_2_out4);
  and and_132 (and_132_out, demultiplexer_1_out3, demultiplexer_2_out4);
  and and_133 (and_133_out, demultiplexer_1_out4, demultiplexer_2_out4);
  and and_134 (and_134_out, demultiplexer_1_out5, demultiplexer_2_out4);
  and and_135 (and_135_out, demultiplexer_1_out6, demultiplexer_2_out4);
  and and_136 (and_136_out, demultiplexer_1_out7, demultiplexer_2_out4);
  assign or_4_out = and_121_out | and_122_out | and_123_out | and_124_out | or_3_out | and_125_out | and_126_out | and_127_out | and_128_out;  // OR_Gate or_4, 16 bits wide
  and and_137 (and_137_out, and_129_out, in_5);
  Memo2byte memo2byte_33 (.in_2(in_4), .in_1(in_3), .in_3(and_137_out), .out_4(memo2byte_33_out_4));
  and and_138 (and_138_out, ~and_137_out, and_129_out);  // AND_Gate
  and and_139 (and_139_out, and_130_out, in_5);
  Memo2byte memo2byte_34 (.in_2(in_4), .in_1(in_3), .in_3(and_139_out), .out_4(memo2byte_34_out_4));
  and and_140 (and_140_out, ~and_139_out, and_130_out);  // AND_Gate
  and and_141 (and_141_out, and_131_out, in_5);
  Memo2byte memo2byte_35 (.in_2(in_4), .in_1(in_3), .in_3(and_141_out), .out_4(memo2byte_35_out_4));
  and and_142 (and_142_out, ~and_141_out, and_131_out);  // AND_Gate
  and and_143 (and_143_out, and_132_out, in_5);
  Memo2byte memo2byte_36 (.in_2(in_4), .in_1(in_3), .in_3(and_143_out), .out_4(memo2byte_36_out_4));
  and and_144 (and_144_out, ~and_143_out, and_132_out);  // AND_Gate
  and and_145 (and_145_out, and_133_out, in_5);
  Memo2byte memo2byte_37 (.in_2(in_4), .in_1(in_3), .in_3(and_145_out), .out_4(memo2byte_37_out_4));
  and and_146 (and_146_out, ~and_145_out, and_133_out);  // AND_Gate
  and and_147 (and_147_out, and_134_out, in_5);
  Memo2byte memo2byte_38 (.in_2(in_4), .in_1(in_3), .in_3(and_147_out), .out_4(memo2byte_38_out_4));
  and and_148 (and_148_out, ~and_147_out, and_134_out);  // AND_Gate
  and and_149 (and_149_out, and_135_out, in_5);
  Memo2byte memo2byte_39 (.in_2(in_4), .in_1(in_3), .in_3(and_149_out), .out_4(memo2byte_39_out_4));
  and and_150 (and_150_out, ~and_149_out, and_135_out);  // AND_Gate
  and and_151 (and_151_out, and_136_out, in_5);
  Memo2byte memo2byte_40 (.in_2(in_4), .in_1(in_3), .in_3(and_151_out), .out_4(memo2byte_40_out_4));
  and and_152 (and_152_out, ~and_151_out, and_136_out);  // AND_Gate
  assign bit_extender_33_out = {{15{and_138_out}}, and_138_out};  // Bit_Extender bit_extender_33
  assign bit_extender_34_out = {{15{and_140_out}}, and_140_out};  // Bit_Extender bit_extender_34
  assign bit_extender_35_out = {{15{and_142_out}}, and_142_out};  // Bit_Extender bit_extender_35
  assign bit_extender_36_out = {{15{and_144_out}}, and_144_out};  // Bit_Extender bit_extender_36
  assign bit_extender_37_out = {{15{and_146_out}}, and_146_out};  // Bit_Extender bit_extender_37
  assign bit_extender_38_out = {{15{and_148_out}}, and_148_out};  // Bit_Extender bit_extender_38
  assign bit_extender_39_out = {{15{and_150_out}}, and_150_out};  // Bit_Extender bit_extender_39
  assign bit_extender_40_out = {{15{and_152_out}}, and_152_out};  // Bit_Extender bit_extender_40
  assign and_153_out = memo2byte_33_out_4 & bit_extender_33_out;  // AND_Gate and_153, 16 bits wide
  assign and_154_out = memo2byte_34_out_4 & bit_extender_34_out;  // AND_Gate and_154, 16 bits wide
  assign and_155_out = memo2byte_35_out_4 & bit_extender_35_out;  // AND_Gate and_155, 16 bits wide
  assign and_156_out = memo2byte_36_out_4 & bit_extender_36_out;  // AND_Gate and_156, 16 bits wide
  assign and_157_out = memo2byte_37_out_4 & bit_extender_37_out;  // AND_Gate and_157, 16 bits wide
  assign and_158_out = memo2byte_38_out_4 & bit_extender_38_out;  // AND_Gate and_158, 16 bits wide
  assign and_159_out = memo2byte_39_out_4 & bit_extender_39_out;  // AND_Gate and_159, 16 bits wide
  assign and_160_out = memo2byte_40_out_4 & bit_extender_40_out;  // AND_Gate and_160, 16 bits wide
  assign or_5_out = and_153_out | and_154_out | and_155_out | and_156_out | or_4_out | and_157_out | and_158_out | and_159_out | and_160_out;  // OR_Gate or_5, 16 bits wide
  and and_161 (and_161_out, demultiplexer_1_out0, demultiplexer_2_out5);
  and and_162 (and_162_out, and_161_out, in_5);
  and and_163 (and_163_out, demultiplexer_1_out1, demultiplexer_2_out5);
  and and_164 (and_164_out, and_163_out, in_5);
  and and_165 (and_165_out, demultiplexer_1_out2, demultiplexer_2_out5);
  and and_166 (and_166_out, and_165_out, in_5);
  and and_167 (and_167_out, demultiplexer_1_out3, demultiplexer_2_out5);
  and and_168 (and_168_out, and_167_out, in_5);
  and and_169 (and_169_out, demultiplexer_1_out4, demultiplexer_2_out5);
  and and_170 (and_170_out, and_169_out, in_5);
  and and_171 (and_171_out, demultiplexer_1_out5, demultiplexer_2_out5);
  and and_172 (and_172_out, and_171_out, in_5);
  and and_173 (and_173_out, demultiplexer_1_out6, demultiplexer_2_out5);
  and and_174 (and_174_out, and_173_out, in_5);
  and and_175 (and_175_out, demultiplexer_1_out7, demultiplexer_2_out5);
  and and_176 (and_176_out, and_175_out, in_5);
  Memo2byte memo2byte_41 (.in_2(in_4), .in_1(in_3), .in_3(and_162_out), .out_4(memo2byte_41_out_4));
  and and_177 (and_177_out, ~and_162_out, and_161_out);  // AND_Gate
  Memo2byte memo2byte_42 (.in_2(in_4), .in_1(in_3), .in_3(and_164_out), .out_4(memo2byte_42_out_4));
  and and_178 (and_178_out, ~and_164_out, and_163_out);  // AND_Gate
  Memo2byte memo2byte_43 (.in_2(in_4), .in_1(in_3), .in_3(and_166_out), .out_4(memo2byte_43_out_4));
  and and_179 (and_179_out, ~and_166_out, and_165_out);  // AND_Gate
  Memo2byte memo2byte_44 (.in_2(in_4), .in_1(in_3), .in_3(and_168_out), .out_4(memo2byte_44_out_4));
  and and_180 (and_180_out, ~and_168_out, and_167_out);  // AND_Gate
  Memo2byte memo2byte_45 (.in_2(in_4), .in_1(in_3), .in_3(and_170_out), .out_4(memo2byte_45_out_4));
  and and_181 (and_181_out, ~and_170_out, and_169_out);  // AND_Gate
  Memo2byte memo2byte_46 (.in_2(in_4), .in_1(in_3), .in_3(and_172_out), .out_4(memo2byte_46_out_4));
  and and_182 (and_182_out, ~and_172_out, and_171_out);  // AND_Gate
  Memo2byte memo2byte_47 (.in_2(in_4), .in_1(in_3), .in_3(and_174_out), .out_4(memo2byte_47_out_4));
  and and_183 (and_183_out, ~and_174_out, and_173_out);  // AND_Gate
  Memo2byte memo2byte_48 (.in_2(in_4), .in_1(in_3), .in_3(and_176_out), .out_4(memo2byte_48_out_4));
  and and_184 (and_184_out, ~and_176_out, and_175_out);  // AND_Gate
  assign and_185_out = memo2byte_41_out_4 & bit_extender_41_out;  // AND_Gate and_185, 16 bits wide
  assign bit_extender_41_out = {{15{and_177_out}}, and_177_out};  // Bit_Extender bit_extender_41
  assign and_186_out = memo2byte_42_out_4 & bit_extender_42_out;  // AND_Gate and_186, 16 bits wide
  assign bit_extender_42_out = {{15{and_178_out}}, and_178_out};  // Bit_Extender bit_extender_42
  assign and_187_out = memo2byte_43_out_4 & bit_extender_43_out;  // AND_Gate and_187, 16 bits wide
  assign bit_extender_43_out = {{15{and_179_out}}, and_179_out};  // Bit_Extender bit_extender_43
  assign and_188_out = memo2byte_44_out_4 & bit_extender_44_out;  // AND_Gate and_188, 16 bits wide
  assign bit_extender_44_out = {{15{and_180_out}}, and_180_out};  // Bit_Extender bit_extender_44
  assign and_189_out = memo2byte_45_out_4 & bit_extender_45_out;  // AND_Gate and_189, 16 bits wide
  assign bit_extender_45_out = {{15{and_181_out}}, and_181_out};  // Bit_Extender bit_extender_45
  assign and_190_out = memo2byte_46_out_4 & bit_extender_46_out;  // AND_Gate and_190, 16 bits wide
  assign bit_extender_46_out = {{15{and_182_out}}, and_182_out};  // Bit_Extender bit_extender_46
  assign and_191_out = memo2byte_47_out_4 & bit_extender_47_out;  // AND_Gate and_191, 16 bits wide
  assign bit_extender_47_out = {{15{and_183_out}}, and_183_out};  // Bit_Extender bit_extender_47
  assign and_192_out = memo2byte_48_out_4 & bit_extender_48_out;  // AND_Gate and_192, 16 bits wide
  assign bit_extender_48_out = {{15{and_184_out}}, and_184_out};  // Bit_Extender bit_extender_48
  and and_193 (and_193_out, demultiplexer_1_out0, demultiplexer_2_out6);
  and and_194 (and_194_out, demultiplexer_1_out1, demultiplexer_2_out6);
  and and_195 (and_195_out, demultiplexer_1_out2, demultiplexer_2_out6);
  and and_196 (and_196_out, demultiplexer_1_out3, demultiplexer_2_out6);
  and and_197 (and_197_out, demultiplexer_1_out4, demultiplexer_2_out6);
  and and_198 (and_198_out, demultiplexer_1_out5, demultiplexer_2_out6);
  and and_199 (and_199_out, demultiplexer_1_out6, demultiplexer_2_out6);
  and and_200 (and_200_out, demultiplexer_1_out7, demultiplexer_2_out6);
  assign or_6_out = and_185_out | and_186_out | and_187_out | and_188_out | or_5_out | and_189_out | and_190_out | and_191_out | and_192_out;  // OR_Gate or_6, 16 bits wide
  buf and_201 (and_201_out, in_5);  // AND_Gate
  and and_202 (and_202_out, and_194_out, in_5);
  buf and_203 (and_203_out, in_5);  // AND_Gate
  and and_204 (and_204_out, and_196_out, in_5);
  buf and_205 (and_205_out, in_5);  // AND_Gate
  and and_206 (and_206_out, and_198_out, in_5);
  buf and_207 (and_207_out, in_5);  // AND_Gate
  and and_208 (and_208_out, and_200_out, in_5);
  Memo2byte memo2byte_49 (.in_2(in_4), .in_1(in_3), .in_3(and_201_out), .out_4(memo2byte_49_out_4));
  assign bit_extender_49_out = {{15{and_209_out}}, and_209_out};  // Bit_Extender bit_extender_49
  and and_209 (and_209_out, ~and_201_out, and_193_out);  // AND_Gate
  Memo2byte memo2byte_50 (.in_2(in_4), .in_1(in_3), .in_3(and_202_out), .out_4(memo2byte_50_out_4));
  assign bit_extender_50_out = {{15{and_210_out}}, and_210_out};  // Bit_Extender bit_extender_50
  and and_210 (and_210_out, ~and_202_out, and_194_out);  // AND_Gate
  Memo2byte memo2byte_51 (.in_2(in_4), .in_1(in_3), .in_3(and_203_out), .out_4(memo2byte_51_out_4));
  assign bit_extender_51_out = {{15{and_211_out}}, and_211_out};  // Bit_Extender bit_extender_51
  and and_211 (and_211_out, ~and_203_out, and_195_out);  // AND_Gate
  Memo2byte memo2byte_52 (.in_2(in_4), .in_1(in_3), .in_3(and_204_out), .out_4(memo2byte_52_out_4));
  assign bit_extender_52_out = {{15{and_212_out}}, and_212_out};  // Bit_Extender bit_extender_52
  and and_212 (and_212_out, ~and_204_out, and_196_out);  // AND_Gate
  Memo2byte memo2byte_53 (.in_2(in_4), .in_1(in_3), .in_3(and_205_out), .out_4(memo2byte_53_out_4));
  assign bit_extender_53_out = {{15{and_213_out}}, and_213_out};  // Bit_Extender bit_extender_53
  and and_213 (and_213_out, ~and_205_out, and_197_out);  // AND_Gate
  Memo2byte memo2byte_54 (.in_2(in_4), .in_1(in_3), .in_3(and_206_out), .out_4(memo2byte_54_out_4));
  assign bit_extender_54_out = {{15{and_214_out}}, and_214_out};  // Bit_Extender bit_extender_54
  and and_214 (and_214_out, ~and_206_out, and_198_out);  // AND_Gate
  Memo2byte memo2byte_55 (.in_2(in_4), .in_1(in_3), .in_3(and_207_out), .out_4(memo2byte_55_out_4));
  assign bit_extender_55_out = {{15{and_215_out}}, and_215_out};  // Bit_Extender bit_extender_55
  and and_215 (and_215_out, ~and_207_out, and_199_out);  // AND_Gate
  Memo2byte memo2byte_56 (.in_2(in_4), .in_1(in_3), .in_3(and_208_out), .out_4(memo2byte_56_out_4));
  assign bit_extender_56_out = {{15{and_216_out}}, and_216_out};  // Bit_Extender bit_extender_56
  and and_216 (and_216_out, ~and_208_out, and_200_out);  // AND_Gate
  assign and_217_out = memo2byte_49_out_4 & bit_extender_49_out;  // AND_Gate and_217, 16 bits wide
  assign and_218_out = memo2byte_50_out_4 & bit_extender_50_out;  // AND_Gate and_218, 16 bits wide
  assign and_219_out = memo2byte_51_out_4 & bit_extender_51_out;  // AND_Gate and_219, 16 bits wide
  assign and_220_out = memo2byte_52_out_4 & bit_extender_52_out;  // AND_Gate and_220, 16 bits wide
  assign and_221_out = memo2byte_53_out_4 & bit_extender_53_out;  // AND_Gate and_221, 16 bits wide
  assign and_222_out = memo2byte_54_out_4 & bit_extender_54_out;  // AND_Gate and_222, 16 bits wide
  assign and_223_out = memo2byte_55_out_4 & bit_extender_55_out;  // AND_Gate and_223, 16 bits wide
  assign and_224_out = memo2byte_56_out_4 & bit_extender_56_out;  // AND_Gate and_224, 16 bits wide
  and and_225 (and_225_out, demultiplexer_1_out0, demultiplexer_2_out7);
  and and_226 (and_226_out, demultiplexer_1_out1, demultiplexer_2_out7);
  and and_227 (and_227_out, demultiplexer_1_out2, demultiplexer_2_out7);
  and and_228 (and_228_out, demultiplexer_1_out3, demultiplexer_2_out7);
  and and_229 (and_229_out, demultiplexer_1_out4, demultiplexer_2_out7);
  and and_230 (and_230_out, demultiplexer_1_out5, demultiplexer_2_out7);
  and and_231 (and_231_out, demultiplexer_1_out6, demultiplexer_2_out7);
  and and_232 (and_232_out, demultiplexer_1_out7, demultiplexer_2_out7);
  assign or_7_out = and_217_out | and_218_out | and_219_out | and_220_out | or_6_out | and_221_out | and_222_out | and_223_out | and_224_out;  // OR_Gate or_7, 16 bits wide
  buf and_233 (and_233_out, in_5);  // AND_Gate
  Memo2byte memo2byte_57 (.in_2(in_4), .in_1(in_3), .in_3(and_233_out), .out_4(memo2byte_57_out_4));
  and and_234 (and_234_out, and_226_out, in_5);
  Memo2byte memo2byte_58 (.in_2(in_4), .in_1(in_3), .in_3(and_234_out), .out_4(memo2byte_58_out_4));
  buf and_235 (and_235_out, in_5);  // AND_Gate
  Memo2byte memo2byte_59 (.in_2(in_4), .in_1(in_3), .in_3(and_235_out), .out_4(memo2byte_59_out_4));
  and and_236 (and_236_out, and_228_out, in_5);
  Memo2byte memo2byte_60 (.in_2(in_4), .in_1(in_3), .in_3(and_236_out), .out_4(memo2byte_60_out_4));
  buf and_237 (and_237_out, in_5);  // AND_Gate
  Memo2byte memo2byte_61 (.in_2(in_4), .in_1(in_3), .in_3(and_237_out), .out_4(memo2byte_61_out_4));
  and and_238 (and_238_out, and_230_out, in_5);
  Memo2byte memo2byte_62 (.in_2(in_4), .in_1(in_3), .in_3(and_238_out), .out_4(memo2byte_62_out_4));
  buf and_239 (and_239_out, in_5);  // AND_Gate
  Memo2byte memo2byte_63 (.in_2(in_4), .in_1(in_3), .in_3(and_239_out), .out_4(memo2byte_63_out_4));
  and and_240 (and_240_out, and_232_out, in_5);
  Memo2byte memo2byte_64 (.in_2(in_4), .in_1(in_3), .in_3(and_240_out), .out_4(memo2byte_64_out_4));
  assign bit_extender_57_out = {{15{and_241_out}}, and_241_out};  // Bit_Extender bit_extender_57
  and and_241 (and_241_out, ~and_233_out, and_225_out);  // AND_Gate
  assign bit_extender_58_out = {{15{and_242_out}}, and_242_out};  // Bit_Extender bit_extender_58
  and and_242 (and_242_out, ~and_234_out, and_226_out);  // AND_Gate
  assign bit_extender_59_out = {{15{and_243_out}}, and_243_out};  // Bit_Extender bit_extender_59
  and and_243 (and_243_out, ~and_235_out, and_227_out);  // AND_Gate
  assign bit_extender_60_out = {{15{and_244_out}}, and_244_out};  // Bit_Extender bit_extender_60
  and and_244 (and_244_out, ~and_236_out, and_228_out);  // AND_Gate
  assign bit_extender_61_out = {{15{and_245_out}}, and_245_out};  // Bit_Extender bit_extender_61
  and and_245 (and_245_out, ~and_237_out, and_229_out);  // AND_Gate
  assign bit_extender_62_out = {{15{and_246_out}}, and_246_out};  // Bit_Extender bit_extender_62
  and and_246 (and_246_out, ~and_238_out, and_230_out);  // AND_Gate
  assign bit_extender_63_out = {{15{and_247_out}}, and_247_out};  // Bit_Extender bit_extender_63
  and and_247 (and_247_out, ~and_239_out, and_231_out);  // AND_Gate
  assign bit_extender_64_out = {{15{and_248_out}}, and_248_out};  // Bit_Extender bit_extender_64
  and and_248 (and_248_out, ~and_240_out, and_232_out);  // AND_Gate
  assign and_249_out = memo2byte_57_out_4 & bit_extender_57_out;  // AND_Gate and_249, 16 bits wide
  assign and_250_out = memo2byte_58_out_4 & bit_extender_58_out;  // AND_Gate and_250, 16 bits wide
  assign and_251_out = memo2byte_59_out_4 & bit_extender_59_out;  // AND_Gate and_251, 16 bits wide
  assign and_252_out = memo2byte_60_out_4 & bit_extender_60_out;  // AND_Gate and_252, 16 bits wide
  assign and_253_out = memo2byte_61_out_4 & bit_extender_61_out;  // AND_Gate and_253, 16 bits wide
  assign and_254_out = memo2byte_62_out_4 & bit_extender_62_out;  // AND_Gate and_254, 16 bits wide
  assign and_255_out = memo2byte_63_out_4 & bit_extender_63_out;  // AND_Gate and_255, 16 bits wide
  assign and_256_out = memo2byte_64_out_4 & bit_extender_64_out;  // AND_Gate and_256, 16 bits wide
  assign out_6 = and_249_out | and_250_out | and_251_out | and_252_out | or_7_out | and_253_out | and_254_out | and_255_out | and_256_out;  // OR_Gate or_8, 16 bits wide
endmodule

module Memo1kB (
  input  in_1,
  input  in_2,
  input  [7:0] in_3,
  input  [15:0] in_4,
  input  in_5,
  output [15:0] out_6
);

  wire demultiplexer_1_out0, demultiplexer_1_out1, demultiplexer_1_out2, demultiplexer_1_out3;
  wire [15:0] memo128byte_1_out_6, memo128byte_2_out_6, memo128byte_3_out_6, memo128byte_4_out_6;

  Demultiplexer #(.select(2)) demultiplexer_1 (
    .out0(demultiplexer_1_out0), .out1(demultiplexer_1_out1), .out2(demultiplexer_1_out2),
    .out3(demultiplexer_1_out3), .in(in_2), .sel(in_3[7:6]));
  Memo128byte memo128byte_1 (
    .in_1(demultiplexer_1_out1), .in_4(in_5), .in_5(in_1), .in_2(in_3[5:0]), .in_3(in_4),
    .out_6(memo128byte_1_out_6));
  Memo128byte memo128byte_2 (
    .in_1(demultiplexer_1_out3), .in_4(in_5), .in_5(in_1), .in_2(in_3[5:0]), .in_3(in_4),
    .out_6(memo128byte_2_out_6));
  Memo128byte memo128byte_3 (
    .in_1(demultiplexer_1_out0), .in_4(in_5), .in_5(in_1), .in_2(in_3[5:0]), .in_3(in_4),
    .out_6(memo128byte_3_out_6));
  Memo128byte memo128byte_4 (
    .in_1(demultiplexer_1_out2), .in_4(in_5), .in_5(in_1), .in_2(in_3[5:0]), .in_3(in_4),
    .out_6(memo128byte_4_out_6));
  assign out_6 = memo128byte_3_out_6 | memo128byte_4_out_6 | memo128byte_1_out_6 | memo128byte_2_out_6;  // OR_Gate or_1, 16 bits wide
endmodule
