// Logisim project REGISTER16BIT.circ as structural Verilog: 2 circuits, main circuit main
module main (
  input  in_1,
  input  [15:0] in_2,
  input  in_3,
  output [15:0] out_4
);

  REGISTER16 register16_1 (.in_1(in_2), .in_2(in_3), .in_3(in_1), .out_4(out_4));
endmodule

module REGISTER16 (
  input  [15:0] in_1,
  input  in_2,
  input  in_3,
  output [15:0] out_4
);

  wire multiplexer_1_out, multiplexer_2_out, multiplexer_3_out, multiplexer_4_out, multiplexer_5_out,
       multiplexer_6_out, multiplexer_7_out, multiplexer_8_out, multiplexer_9_out, multiplexer_10_out,
       multiplexer_11_out, multiplexer_12_out, multiplexer_13_out, multiplexer_14_out, multiplexer_15_out,
       multiplexer_16_out;

  D_Flip_Flop d_ff_1 (.D(multiplexer_1_out), .clk(in_2), .Q(out_4[15]));  // open: Qn, preset, reset
  Multiplexer multiplexer_1 (.in0(out_4[15]), .in1(in_1[15]), .out(multiplexer_1_out), .sel(in_3));
  Multiplexer multiplexer_2 (.in0(out_4[14]), .in1(in_1[14]), .out(multiplexer_2_out), .sel(in_3));
  D_Flip_Flop d_ff_2 (.D(multiplexer_2_out), .clk(in_2), .Q(out_4[14]));  // open: Qn, preset, reset
  D_Flip_Flop d_ff_3 (.D(multiplexer_3_out), .clk(in_2), .Q(out_4[13]));  // open: Qn, preset, reset
  Multiplexer multiplexer_3 (.in0(out_4[13]), .in1(in_1[13]), .out(multiplexer_3_out), .sel(in_3));
  D_Flip_Flop d_ff_4 (.D(multiplexer_4_out), .clk(in_2), .Q(out_4[12]));  // open: Qn, preset, reset
  Multiplexer multiplexer_4 (.in0(out_4[12]), .in1(in_1[12]), .out(multiplexer_4_out), .sel(in_3));
  D_Flip_Flop d_ff_5 (.D(multiplexer_5_out), .clk(in_2), .Q(out_4[11]));  // open: Qn, preset, reset
  Multiplexer multiplexer_5 (.in0(out_4[11]), .in1(in_1[11]), .out(multiplexer_5_out), .sel(in_3));
  Multiplexer multiplexer_6 (.in0(out_4[10]), .in1(in_1[10]), .out(multiplexer_6_out), .sel(in_3));
  D_Flip_Flop d_ff_6 (.D(multiplexer_6_out), .clk(in_2), .Q(out_4[10]));  // open: Qn, preset, reset
  D_Flip_Flop d_ff_7 (.D(multiplexer_7_out), .clk(in_2), .Q(out_4[9]));  // open: Qn, preset, reset
  Multiplexer multiplexer_7 (.in0(out_4[9]), .in1(in_1[9]), .out(multiplexer_7_out), .sel(in_3));
  D_Flip_Flop d_ff_8 (.D(multiplexer_8_out), .clk(in_2), .Q(out_4[8]));  // open: Qn, preset, reset
  Multiplexer multiplexer_8 (.in0(out_4[8]), .in1(in_1[8]), .out(multiplexer_8_out), .sel(in_3));
  D_Flip_Flop d_ff_9 (.D(multiplexer_9_out), .clk(in_2), .Q(out_4[7]));  // open: Qn, preset, reset
  Multiplexer multiplexer_9 (.in0(out_4[7]), .in1(in_1[7]), .out(multiplexer_9_out), .sel(in_3));
  Multiplexer multiplexer_10 (.in0(out_4[6]), .in1(in_1[6]), .out(multiplexer_10_out), .sel(in_3));
  D_Flip_Flop d_ff_10 (.D(multiplexer_10_out), .clk(in_2), .Q(out_4[6]));  // open: Qn, preset, reset
  D_Flip_Flop d_ff_11 (.D(multiplexer_11_out), .clk(in_2), .Q(out_4[5]));  // open: Qn, preset, reset
  Multiplexer multiplexer_11 (.in0(out_4[5]), .in1(in_1[5]), .out(multiplexer_11_out), .sel(in_3));
  D_Flip_Flop d_ff_12 (.D(multiplexer_12_out), .clk(in_2), .Q(out_4[4]));  // open: Qn, preset, reset
  Multiplexer multiplexer_12 (.in0(out_4[4]), .in1(in_1[4]), .out(multiplexer_12_out), .sel(in_3));
  D_Flip_Flop d_ff_13 (.D(multiplexer_13_out), .clk(in_2), .Q(out_4[3]));  // open: Qn, preset, reset
  Multiplexer multiplexer_13 (.in0(out_4[3]), .in1(in_1[3]), .out(multiplexer_13_out), .sel(in_3));
  Multiplexer multiplexer_14 (.in0(out_4[2]), .in1(in_1[2]), .out(multiplexer_14_out), .sel(in_3));
  D_Flip_Flop d_ff_14 (.D(multiplexer_14_out), .clk(in_2), .Q(out_4[2]));  // open: Qn, preset, reset
  D_Flip_Flop d_ff_15 (.D(multiplexer_15_out), .clk(in_2), .Q(out_4[1]));  // open: Qn, preset, reset
  Multiplexer multiplexer_15 (.in0(out_4[1]), .in1(in_1[1]), .out(multiplexer_15_out), .sel(in_3));
  D_Flip_Flop d_ff_16 (.D(multiplexer_16_out), .clk(in_2), .Q(out_4[0]));  // open: Qn, preset, reset
  Multiplexer multiplexer_16 (.in0(out_4[0]), .in1(in_1[0]), .out(multiplexer_16_out), .sel(in_3));
endmodule
