// Logisim project computer.circ as structural Verilog: 2 circuits, main circuit computer
module computer (
  input  in_1
);

  wire cpu_1_writem;
  wire [14:0] cpu_1_addressm;
  wire [15:0] cpu_1_aluout, cpu_1_prc, rom_1_data, undriven;

  ROM #(.addrWidth(16), .dataWidth(16)) rom_1 (.addr(cpu_1_prc), .data(rom_1_data));
  CPU cpu_1 (
    .INSTRUCTION(rom_1_data), .inM(undriven), .RESET(in_1), .ALUout(cpu_1_aluout), .PRC(cpu_1_prc),
    .WriteM(cpu_1_writem), .AddressM(cpu_1_addressm));

  // Notes on the sheet:
  //   contents of rom_1 (hex, n*v repeats v):
  //   6fff ee88
endmodule

module computerMemo (
  input  in_1
);

  wire and_1_out, clock_1_out, comparator_1_eq, comparator_1_gt, comparator_2_eq, cpu_1_writem, not_1_out,
       or_1_out;
  wire [1:0] pull_resistor_1_node;
  wire [7:0] shifter_1_out;
  wire [8:0] shifter_1_out_2;
  wire [14:0] cpu_1_addressm, subtractor_1_out;
  wire [15:0] cpu_1_aluout, cpu_1_prc, keyboard_1_data, multiplexer_1_out, ram_1_dout, rom_1_data;

  ROM #(.addrWidth(16), .dataWidth(16)) rom_1 (.addr(cpu_1_prc), .data(rom_1_data));
  CPU cpu_1 (
    .INSTRUCTION(rom_1_data), .inM(multiplexer_1_out), .RESET(in_1), .ALUout(cpu_1_aluout), .PRC(cpu_1_prc),
    .WriteM(cpu_1_writem), .AddressM(cpu_1_addressm));
  Comparator #(.mode("unsigned"), .width(15)) comparator_1 (
    .a(cpu_1_addressm), .b(15'h4000), .gt(comparator_1_gt), .eq(comparator_1_eq));  // open: lt
  Comparator #(.mode("unsigned"), .width(15)) comparator_2 (
    .a(cpu_1_addressm), .b(15'h6000), .eq(comparator_2_eq));  // open: gt, lt
  Subtractor #(.width(15)) subtractor_1 (.a(cpu_1_addressm), .b(15'h4000), .out(subtractor_1_out));  // open: bin, bout
  Keyboard #(.buflen(1)) keyboard_1 (.clk(clock_1_out), .data(keyboard_1_data[6:0]));  // open: re, clr, avail
  or or_1 (or_1_out, comparator_1_gt, comparator_1_eq);
  not not_1 (not_1_out, comparator_2_eq);
  and and_1 (and_1_out, or_1_out, not_1_out);
  Pull_Resistor pull_resistor_1 (.node(pull_resistor_1_node));
  Shifter #(.width(17)) shifter_1 (
    .in({pull_resistor_1_node, subtractor_1_out}), .\dist (5'b00100), .out({shifter_1_out, shifter_1_out_2}));
  RAM #(.addrWidth(15), .clearpin("true"), .dataWidth(16), .enables("line")) ram_1 (
    .addr(cpu_1_addressm), .we(cpu_1_writem), .clk(clock_1_out), .din(cpu_1_aluout), .dout(ram_1_dout),
    .clr(in_1));
  Clock clock_1 (.out(clock_1_out));
  // RGB_Video #(.cursor("No Cursor"), .height(256), .width(512), .writemode("Packed 16 (1bpp)")) rgb_video_1: pin names not known; wires that end beside it: in_1, clock_1_out, and_1_out, shifter_1_out_2, shifter_1_out, cpu_1_aluout
  Multiplexer #(.width(16)) multiplexer_1 (
    .in0(ram_1_dout), .in1(keyboard_1_data), .out(multiplexer_1_out), .sel(comparator_2_eq));
  // Pins of 7 and 16 bits meet at keyboard_1_data

  // Notes on the sheet:
  //   contents of rom_1 (hex, n*v repeats v):
  //   4000 ec10 a e308 8 ec10 b e308 a f018 e300 a fde0 2 e090 a e308 b e310 a fc10 8 e390 c e308 c ea87 d
  //   ea87
endmodule
